// Logisim project 网安本硕博2101班-U202112209-吴泽皓-电梯控制器实验电路.circ as structural Verilog: 24 circuits, main circuit 七段数码管
module \七段数码管  (
  input  X3,
  input  X2,
  input  X1,
  input  X0,
  output Seg_1,
  output Seg_2,
  output Seg_3,
  output Seg_4,
  output Seg_5,
  output Seg_6,
  output Seg_7
);

  wire and_1_out, and_2_out, and_3_out, and_4_out, and_5_out, and_6_out, and_7_out, and_8_out, and_9_out,
       and_10_out, and_11_out, and_12_out, and_13_out, and_14_out, and_15_out, and_16_out, not_1_out,
       not_2_out, not_3_out, not_4_out, not_5_out, not_6_out, not_7_out, not_8_out, not_9_out, not_10_out,
       not_11_out, not_12_out, not_13_out, not_14_out, not_15_out, not_16_out, not_17_out, not_18_out,
       not_19_out, not_20_out, not_21_out;

  not not_1 (not_1_out, X2);
  and and_1 (and_1_out, not_1_out, X1);
  and and_2 (and_2_out, X2, not_2_out);
  not not_2 (not_2_out, X1);
  and and_3 (and_3_out, X2, not_3_out);
  not not_3 (not_3_out, X0);
  not not_4 (not_4_out, X1);
  and and_4 (and_4_out, not_4_out, not_5_out);
  not not_5 (not_5_out, X0);
  and and_5 (and_5_out, X2, not_6_out);
  not not_6 (not_6_out, X1);
  and and_6 (and_6_out, X2, not_7_out);
  not not_7 (not_7_out, X0);
  not not_8 (not_8_out, X2);
  and and_7 (and_7_out, not_8_out, not_9_out);
  not not_9 (not_9_out, X0);
  and and_8 (and_8_out, X2, X0);
  not not_10 (not_10_out, X2);
  not not_11 (not_11_out, X1);
  and and_9 (and_9_out, not_11_out, not_12_out);
  not not_12 (not_12_out, X0);
  and and_10 (and_10_out, X1, X0);
  not not_13 (not_13_out, X2);
  and and_11 (and_11_out, not_13_out, not_14_out);
  not not_14 (not_14_out, X0);
  and and_12 (and_12_out, X1, not_15_out);
  not not_15 (not_15_out, X0);
  not not_16 (not_16_out, X2);
  and and_13 (and_13_out, not_16_out, not_17_out);
  not not_17 (not_17_out, X0);
  not not_18 (not_18_out, X2);
  and and_14 (and_14_out, not_18_out, X1);
  and and_15 (and_15_out, X1, not_19_out);
  not not_19 (not_19_out, X0);
  and and_16 (and_16_out, X2, not_20_out, X0);
  not not_20 (not_20_out, X1);
  not not_21 (not_21_out, X1);
  or or_1 (Seg_7, not_21_out, X0, X2);
  or or_2 (Seg_1, and_1_out, and_2_out, and_3_out, X3);
  or or_3 (Seg_2, and_4_out, and_5_out, and_6_out, X3);
  or or_4 (Seg_3, and_7_out, X1, and_8_out, X3);
  or or_5 (Seg_4, not_10_out, and_9_out, and_10_out);
  or or_6 (Seg_5, and_11_out, and_12_out);
  or or_7 (Seg_6, and_13_out, and_14_out, and_15_out, and_16_out, X3);
endmodule

module \七段数码管测试  (
  output [15:0] Cnt,
  output [3:0] BCD,
  output [6:0] _7Segs,
  output _passed,
  output halt
);

  wire and_1_out, CLK, d_ff_1_q, d_ff_1_qn, NEQ, nHalt;
  wire [6:0] _7SegsS;
  wire [9:0] counter_2_q;
  wire [15:0] multiplexer_1_out, multiplexer_1_out_2;
  wire [31:0] XY;

  Clock #(.highDuration(1), .lowDuration(1)) clock_1 (.out(CLK));
  Counter #(.width(16), .max('hffff), .ongoal("wrap"), .trigger("rising"), .behavior("old")) counter_1 (
    .count(nHalt), .Q(Cnt), .clk(CLK));  // open: load, D, carry, clr, preset
  // Probe on Cnt
  // Probe on Cnt
  // Probe on 16'ha
  Comparator #(.width(16), .mode("twosComplement")) comparator_1 (.a(Cnt), .b(16'ha), .eq(halt));  // open: gt, lt
  ROM #(.addrWidth(16), .dataWidth(4), .Select("high")) rom_1 (.addr(Cnt), .data(BCD));
  ROM #(.addrWidth(16), .dataWidth(7), .Select("high")) rom_2 (.addr(Cnt), .data(_7SegsS));
  not not_1 (nHalt, halt);
  RAM #(.addrWidth(16), .dataWidth(7), .bus("separate"), .Select("low")) ram_1 (
    .addr(Cnt), .din(_7Segs), .str(nHalt), .clk(CLK));  // open: data, sel, ld, clr
  not not_2 (NEQ, _passed);
  // 七段数码管 七段数码管_1: pin names not known; wires that end beside it: BCD[3], BCD[2], BCD[1], BCD[0], _7Segs[0], _7Segs[1], _7Segs[2], _7Segs[3], _7Segs[4], _7Segs[5], _7Segs[6]
  LED #(.active("true")) \u_测试完成  (.in(halt));
  Counter #(.width(10), .max('h3ff), .ongoal("wrap"), .trigger("rising"), .behavior("old")) counter_2 (
    .count(NEQ), .Q(counter_2_q), .clk(CLK), .clr(halt));  // open: load, D, carry, preset
  Pull_Resistor #(.pull(0)) pull_resistor_1 (.node(_passed));
  Comparator #(.width(7), .mode("twosComplement")) comparator_2 (
    .a(_7Segs), .b(_7SegsS), .eq(_passed));  // open: gt, lt
  and and_1 (and_1_out, ~halt, NEQ);  // AND_Gate
  RAM #(.addrWidth(10), .dataWidth(32), .bus("separate"), .Select("high")) ram_2 (
    .addr(counter_2_q), .din(XY), .str(and_1_out), .clk(CLK));  // open: data, sel, ld, clr
  _7_Segment_Display #(.active("true")) u_7_segment_display_1 (
    .g(multiplexer_1_out[15]), .f(multiplexer_1_out[14]), .a(multiplexer_1_out[13]),
    .b(multiplexer_1_out[12]), .e(multiplexer_1_out_2[15]), .d(multiplexer_1_out_2[14]),
    .c(multiplexer_1_out_2[13]), .dp(multiplexer_1_out_2[12]));
  _7_Segment_Display #(.active("true")) u_7_segment_display_2 (
    .g(multiplexer_1_out[11]), .f(multiplexer_1_out[10]), .a(multiplexer_1_out[9]), .b(multiplexer_1_out[8]),
    .e(multiplexer_1_out_2[11]), .d(multiplexer_1_out_2[10]), .c(multiplexer_1_out_2[9]),
    .dp(multiplexer_1_out_2[8]));
  _7_Segment_Display #(.active("true")) u_7_segment_display_3 (
    .g(multiplexer_1_out[7]), .f(multiplexer_1_out[6]), .a(multiplexer_1_out[5]), .b(multiplexer_1_out[4]),
    .e(multiplexer_1_out_2[7]), .d(multiplexer_1_out_2[6]), .c(multiplexer_1_out_2[5]),
    .dp(multiplexer_1_out_2[4]));
  D_Flip_Flop #(.trigger("rising"), .Pre_Clr_Positions("LEGACY"), .NegatePresetClear("false"), .enable("true"), .NewFFLayout("false")) d_ff_1 (
    .clk(CLK), .D(NEQ), .Q(d_ff_1_q), .Qn(d_ff_1_qn), .en(d_ff_1_qn));  // open: preset, reset
  _7_Segment_Display #(.active("true")) u_7_segment_display_4 (
    .g(multiplexer_1_out[3]), .f(multiplexer_1_out[2]), .a(multiplexer_1_out[1]), .b(multiplexer_1_out[0]),
    .e(multiplexer_1_out_2[3]), .d(multiplexer_1_out_2[2]), .c(multiplexer_1_out_2[1]),
    .dp(multiplexer_1_out_2[0]));
  Multiplexer #(.select(1), .width(32), .disabled(0), .enable("true")) multiplexer_1 (
    .in0(32'h8a66ffee), .in1(32'h8a8cef44), .out({multiplexer_1_out_2, multiplexer_1_out}), .sel(d_ff_1_q),
    .en(halt));

  // Other names for the same wires on the sheet: Equal = _passed; tunnel[15:0] = Cnt

  // Notes on the sheet:
  //   测试节拍数
  //   contents of rom_1 (hex, n*v repeats v):
  //   0 1 2 3 4 5 6 7 8 9
  //   contents of rom_2 (hex, n*v repeats v):
  //   7e 48 3d 6d 4b 67 77 4c 7f 6f 7e
  //   错误记录X&Y
  //   存储器保存未通过的测试用例
  //   ctrl+K驱动时钟自动测试
endmodule

module \二位无符号比较器  (
  input  X1,
  input  X0,
  input  Y1,
  input  Y0,
  output Great,
  output Equal,
  output Less
);

  wire and_1_out, and_2_out, and_3_out, and_4_out, and_5_out, and_6_out, and_7_out, and_8_out, and_9_out,
       and_10_out, not_1_out, not_2_out, not_3_out, not_4_out, not_5_out, not_6_out, not_7_out, not_8_out,
       not_9_out, not_10_out, not_11_out, not_12_out, not_13_out, not_14_out, not_15_out, not_16_out;

  not not_1 (not_1_out, Y1);
  and and_1 (and_1_out, X0, not_1_out, not_2_out);
  not not_2 (not_2_out, Y0);
  and and_2 (and_2_out, X1, not_3_out);
  not not_3 (not_3_out, Y1);
  and and_3 (and_3_out, X1, X0, not_4_out);
  not not_4 (not_4_out, Y0);
  not not_5 (not_5_out, X1);
  not not_6 (not_6_out, X0);
  not not_7 (not_7_out, Y1);
  not not_8 (not_8_out, Y0);
  not not_9 (not_9_out, X1);
  not not_10 (not_10_out, Y1);
  not not_11 (not_11_out, X0);
  not not_12 (not_12_out, Y0);
  not not_13 (not_13_out, X1);
  not not_14 (not_14_out, X0);
  and and_4 (and_4_out, not_13_out, not_14_out, Y0);
  not not_15 (not_15_out, X1);
  and and_5 (and_5_out, not_15_out, Y1);
  not not_16 (not_16_out, X0);
  and and_6 (and_6_out, not_16_out, Y1, Y0);
  or or_1 (Great, and_1_out, and_2_out, and_3_out);
  and and_7 (and_7_out, not_5_out, not_6_out, not_7_out, not_8_out);
  and and_8 (and_8_out, not_9_out, X0, not_10_out, Y0);
  and and_9 (and_9_out, X1, not_11_out, Y1, not_12_out);
  and and_10 (and_10_out, X1, X0, Y1, Y0);
  or or_2 (Less, and_4_out, and_5_out, and_6_out);
  or or_3 (Equal, and_7_out, and_8_out, and_9_out, and_10_out);
endmodule

module \二位无符号比较器测试  (
  output [15:0] Cnt,
  output X0,
  output X1,
  output Y0,
  output Y1,
  output [2:0] Out,
  output _passed,
  output halt
);

  wire and_1_out, CLK, d_ff_1_q, d_ff_1_qn, NEQ, nHalt;
  wire [2:0] OutS;
  wire [9:0] counter_2_q;
  wire [15:0] multiplexer_1_out, multiplexer_1_out_2;
  wire [31:0] XY;

  Clock #(.highDuration(1), .lowDuration(1)) clock_1 (.out(CLK));
  Counter #(.width(16), .max('hffff), .ongoal("wrap"), .trigger("rising"), .behavior("old")) counter_1 (
    .count(nHalt), .Q(Cnt), .clk(CLK));  // open: load, D, carry, clr, preset
  // Probe on Cnt
  // Probe on Cnt
  // Probe on 16'hf
  Comparator #(.width(16), .mode("twosComplement")) comparator_1 (.a(Cnt), .b(16'hf), .eq(halt));  // open: gt, lt
  ROM #(.addrWidth(16), .dataWidth(4), .Select("high")) rom_1 (.addr(Cnt), .data({Y1, Y0, X1, X0}));
  ROM #(.addrWidth(16), .dataWidth(3), .Select("high")) rom_2 (.addr(Cnt), .data(OutS));
  not not_1 (nHalt, halt);
  RAM #(.addrWidth(16), .dataWidth(3), .bus("separate"), .Select("low")) ram_1 (
    .addr(Cnt), .din(Out), .str(nHalt), .clk(CLK));  // open: data, sel, ld, clr
  not not_2 (NEQ, _passed);
  // 二位无符号比较器 二位无符号比较器_1: pin names not known; wires that end beside it: X1, X0, Y1, Y0, Out[0], Out[1], Out[2]
  Comparator #(.width(3), .mode("unsigned")) comparator_2 (.a(Out), .b(OutS), .eq(_passed));  // open: gt, lt
  LED #(.active("true")) \u_测试完成  (.in(halt));
  Counter #(.width(10), .max('h3ff), .ongoal("wrap"), .trigger("rising"), .behavior("old")) counter_2 (
    .count(NEQ), .Q(counter_2_q), .clk(CLK), .clr(halt));  // open: load, D, carry, preset
  Pull_Resistor #(.pull(0)) pull_resistor_1 (.node(_passed));
  and and_1 (and_1_out, ~halt, NEQ);  // AND_Gate
  RAM #(.addrWidth(10), .dataWidth(32), .bus("separate"), .Select("high")) ram_2 (
    .addr(counter_2_q), .din(XY), .str(and_1_out), .clk(CLK));  // open: data, sel, ld, clr
  _7_Segment_Display #(.active("true")) u_7_segment_display_1 (
    .g(multiplexer_1_out[15]), .f(multiplexer_1_out[14]), .a(multiplexer_1_out[13]),
    .b(multiplexer_1_out[12]), .e(multiplexer_1_out_2[15]), .d(multiplexer_1_out_2[14]),
    .c(multiplexer_1_out_2[13]), .dp(multiplexer_1_out_2[12]));
  _7_Segment_Display #(.active("true")) u_7_segment_display_2 (
    .g(multiplexer_1_out[7]), .f(multiplexer_1_out[6]), .a(multiplexer_1_out[5]), .b(multiplexer_1_out[4]),
    .e(multiplexer_1_out_2[7]), .d(multiplexer_1_out_2[6]), .c(multiplexer_1_out_2[5]),
    .dp(multiplexer_1_out_2[4]));
  _7_Segment_Display #(.active("true")) u_7_segment_display_3 (
    .g(multiplexer_1_out[11]), .f(multiplexer_1_out[10]), .a(multiplexer_1_out[9]), .b(multiplexer_1_out[8]),
    .e(multiplexer_1_out_2[11]), .d(multiplexer_1_out_2[10]), .c(multiplexer_1_out_2[9]),
    .dp(multiplexer_1_out_2[8]));
  D_Flip_Flop #(.trigger("rising"), .Pre_Clr_Positions("LEGACY"), .NegatePresetClear("false"), .enable("true"), .NewFFLayout("false")) d_ff_1 (
    .clk(CLK), .D(NEQ), .Q(d_ff_1_q), .Qn(d_ff_1_qn), .en(d_ff_1_qn));  // open: preset, reset
  _7_Segment_Display #(.active("true")) u_7_segment_display_4 (
    .g(multiplexer_1_out[3]), .f(multiplexer_1_out[2]), .a(multiplexer_1_out[1]), .b(multiplexer_1_out[0]),
    .e(multiplexer_1_out_2[3]), .d(multiplexer_1_out_2[2]), .c(multiplexer_1_out_2[1]),
    .dp(multiplexer_1_out_2[0]));
  Multiplexer #(.select(1), .width(32), .disabled(0), .enable("true")) multiplexer_1 (
    .in0(32'h8a66ffee), .in1(32'h8a8cef44), .out({multiplexer_1_out_2, multiplexer_1_out}), .sel(d_ff_1_q),
    .en(halt));

  // Other names for the same wires on the sheet: Equal = _passed; Input[3:0] = {Y1, Y0, X1, X0}; tunnel[15:0] = Cnt

  // Notes on the sheet:
  //   测试节拍数
  //   contents of rom_1 (hex, n*v repeats v):
  //   0 1 2 3 4 5 6 7 8 9 a b c d e f
  //   contents of rom_2 (hex, n*v repeats v):
  //   2 1 1 1 4 2 1 1 4 4 2 1 4 4 4 2
  //   错误记录X&Y
  //   存储器保存未通过的测试用例
  //   ctrl+K驱动时钟自动测试
endmodule

module \请求和取消请求  (
  input  \楼层低位 ,
  input  \内部1楼请求 ,
  input  \外部1楼上 ,
  input  \外部2楼下 ,
  input  \楼层高位 ,
  input  \内部2楼请求 ,
  input  \外部2楼上 ,
  input  \外部3楼下 ,
  input  \内部3楼请求 ,
  input  \开门 ,
  input  \外部3楼上 ,
  input  \外部4楼下 ,
  input  \上升 ,
  input  \内部4楼请求 ,
  input  \下降 ,
  input  \开门_2 ,
  input  \关门 ,
  output \内部1楼请求_2 ,
  output \_1楼上请求 ,
  output \_2楼下请求 ,
  output \内部2楼请求_2 ,
  output \_2楼上请求 ,
  output \_3楼下请求 ,
  output \内部3楼请求_2 ,
  output \_3楼上请求 ,
  output \_4楼下请求 ,
  output \内部4楼请求_2 ,
  output \手动开门请求 ,
  output \手动关门请求 
);

  wire and_1_out, and_2_out, and_3_out, and_4_out, and_5_out, and_6_out, and_7_out, and_8_out, and_9_out,
       and_10_out, and_11_out, and_12_out, nor_1_out, nor_2_out, not_1_out, or_1_out, or_2_out, or_3_out,
       or_4_out, \二位无符号比较器_1_equal , \二位无符号比较器_2_equal , \二位无符号比较器_3_equal , \二位无符号比较器_4_equal ;

  T_Flip_Flop #(.trigger("rising"), .Pre_Clr_Positions("ABOVE_BELOW"), .NegatePresetClear("false"), .enable("false"), .NewFFLayout("true")) t_ff_1 (
    .clk(\内部1楼请求 ), .T(\内部1楼请求 ), .Q(\内部1楼请求_2 ), .reset(and_1_out));  // open: Qn, preset
  \二位无符号比较器  \u_二位无符号比较器_1  (
    .X1(\楼层高位 ), .X0(\楼层低位 ), .Y1(1'b0), .Y0(1'b0), .Equal(\二位无符号比较器_1_equal ));  // open: Great, Less
  T_Flip_Flop #(.trigger("rising"), .Pre_Clr_Positions("ABOVE_BELOW"), .NegatePresetClear("false"), .enable("false"), .NewFFLayout("true")) t_ff_2 (
    .clk(\内部3楼请求 ), .T(\内部3楼请求 ), .Q(\内部3楼请求_2 ), .reset(and_3_out));  // open: Qn, preset
  \二位无符号比较器  \u_二位无符号比较器_2  (
    .X1(\楼层高位 ), .X0(\楼层低位 ), .Y1(1'b1), .Y0(1'b0), .Equal(\二位无符号比较器_2_equal ));  // open: Great, Less
  and and_1 (and_1_out, \二位无符号比较器_1_equal , \开门 );
  and and_2 (and_2_out, and_3_out, \上升 );
  and and_3 (and_3_out, \二位无符号比较器_2_equal , \开门 );
  D_Flip_Flop #(.trigger("rising"), .Pre_Clr_Positions("ABOVE_BELOW"), .NegatePresetClear("false"), .enable("false"), .NewFFLayout("true")) d_ff_1 (
    .clk(\开门_2 ), .D(\开门_2 ), .Q(\手动开门请求 ), .reset(\开门 ));  // open: Qn, preset
  T_Flip_Flop #(.trigger("rising"), .Pre_Clr_Positions("ABOVE_BELOW"), .NegatePresetClear("false"), .enable("false"), .NewFFLayout("true")) t_ff_3 (
    .clk(\外部3楼上 ), .T(\外部3楼上 ), .Q(\_3楼上请求 ), .reset(or_1_out));  // open: Qn, preset
  or or_1 (or_1_out, and_2_out, and_4_out);
  T_Flip_Flop #(.trigger("rising"), .Pre_Clr_Positions("ABOVE_BELOW"), .NegatePresetClear("false"), .enable("false"), .NewFFLayout("true")) t_ff_4 (
    .clk(\外部1楼上 ), .T(\外部1楼上 ), .Q(\_1楼上请求 ), .reset(and_1_out));  // open: Qn, preset
  and and_4 (and_4_out, and_3_out, nor_1_out);
  nor nor_1 (nor_1_out, \上升 , \下降 );
  and and_5 (and_5_out, nor_1_out, and_3_out);
  T_Flip_Flop #(.trigger("rising"), .Pre_Clr_Positions("ABOVE_BELOW"), .NegatePresetClear("false"), .enable("false"), .NewFFLayout("true")) t_ff_5 (
    .clk(\内部2楼请求 ), .T(\内部2楼请求 ), .Q(\内部2楼请求_2 ), .reset(and_7_out));  // open: Qn, preset
  T_Flip_Flop #(.trigger("rising"), .Pre_Clr_Positions("ABOVE_BELOW"), .NegatePresetClear("false"), .enable("false"), .NewFFLayout("true")) t_ff_6 (
    .clk(\外部3楼下 ), .T(\外部3楼下 ), .Q(\_3楼下请求 ), .reset(or_2_out));  // open: Qn, preset
  or or_2 (or_2_out, and_5_out, and_6_out);
  and and_6 (and_6_out, and_3_out, \下降 );
  and and_7 (and_7_out, \二位无符号比较器_3_equal , \开门 );
  \二位无符号比较器  \u_二位无符号比较器_3  (
    .X1(\楼层高位 ), .X0(\楼层低位 ), .Y1(1'b0), .Y0(1'b1), .Equal(\二位无符号比较器_3_equal ));  // open: Great, Less
  and and_8 (and_8_out, and_7_out, \上升 );
  or or_3 (or_3_out, and_8_out, and_9_out);
  T_Flip_Flop #(.trigger("rising"), .Pre_Clr_Positions("ABOVE_BELOW"), .NegatePresetClear("false"), .enable("false"), .NewFFLayout("true")) t_ff_7 (
    .clk(\外部2楼上 ), .T(\外部2楼上 ), .Q(\_2楼上请求 ), .reset(or_3_out));  // open: Qn, preset
  and and_9 (and_9_out, and_7_out, nor_2_out);
  T_Flip_Flop #(.trigger("rising"), .Pre_Clr_Positions("ABOVE_BELOW"), .NegatePresetClear("false"), .enable("false"), .NewFFLayout("true")) t_ff_8 (
    .clk(\内部4楼请求 ), .T(\内部4楼请求 ), .Q(\内部4楼请求_2 ), .reset(and_10_out));  // open: Qn, preset
  D_Flip_Flop #(.trigger("rising"), .Pre_Clr_Positions("ABOVE_BELOW"), .NegatePresetClear("false"), .enable("false"), .NewFFLayout("true")) d_ff_2 (
    .clk(\关门 ), .D(\关门 ), .Q(\手动关门请求 ), .reset(not_1_out));  // open: Qn, preset
  not not_1 (not_1_out, \开门 );
  nor nor_2 (nor_2_out, \上升 , \下降 );
  and and_10 (and_10_out, \二位无符号比较器_4_equal , \开门 );
  \二位无符号比较器  \u_二位无符号比较器_4  (
    .X1(\楼层高位 ), .X0(\楼层低位 ), .Y1(1'b1), .Y0(1'b1), .Equal(\二位无符号比较器_4_equal ));  // open: Great, Less
  or or_4 (or_4_out, and_11_out, and_12_out);
  and and_11 (and_11_out, nor_2_out, and_7_out);
  // Probe on {\楼层高位 , \楼层低位 }
  T_Flip_Flop #(.trigger("rising"), .Pre_Clr_Positions("ABOVE_BELOW"), .NegatePresetClear("false"), .enable("false"), .NewFFLayout("true")) t_ff_9 (
    .clk(\外部2楼下 ), .T(\外部2楼下 ), .Q(\_2楼下请求 ), .reset(or_4_out));  // open: Qn, preset
  and and_12 (and_12_out, and_7_out, \下降 );
  T_Flip_Flop #(.trigger("rising"), .Pre_Clr_Positions("ABOVE_BELOW"), .NegatePresetClear("false"), .enable("false"), .NewFFLayout("true")) t_ff_10 (
    .clk(\外部4楼下 ), .T(\外部4楼下 ), .Q(\_4楼下请求 ), .reset(and_10_out));  // open: Qn, preset

  // Other names for the same wires on the sheet: _1楼 = \内部1楼请求 ; _1楼上 = \外部1楼上 ; _1楼请求 = \内部1楼请求_2 ; _2楼 = \内部2楼请求 ;
  //   _2楼上 = \外部2楼上 ; _2楼下 = \外部2楼下 ; _2楼请求 = \内部2楼请求_2 ; _3楼 = \内部3楼请求 ; _3楼上 = \外部3楼上 ; _3楼下 = \外部3楼下 ;
  //   _3楼请求 = \内部3楼请求_2 ; _4楼 = \内部4楼请求 ; _4楼下 = \外部4楼下 ; _4楼请求 = \内部4楼请求_2 ; 当前楼层[1:0] = {\楼层高位 , \楼层低位 };
  //   手动关门 = \关门 ; 手动开门 = \开门_2 

  // Notes on the sheet:
  //   内部输入
  //   一层信号处理
  //   三层信号处理
  //   外部输入
  //   输出
  //   开关门信号处理
  //   二层信号处理
  //   其他输入
  //   四层信号处理
endmodule

module \请求和取消请求测试  (
  output [15:0] Cnt,
  output [1:0] \当前楼层 ,
  output [3:0] \内部按钮 ,
  output [2:0] \外部上按钮 ,
  output [2:0] \外部下按钮 ,
  output [1:0] \开关门按钮 ,
  output [1:0] \上下行输入 ,
  output \门开启_关闭 ,
  output [3:0] \内部请求 ,
  output [2:0] \外部上请求 ,
  output [2:0] \外部下请求 ,
  output [1:0] \开关门请求 ,
  output _passed,
  output halt
);

  wire and_1_out, CLK, d_ff_1_q, d_ff_1_qn, NEQ, nHalt;
  wire [9:0] counter_2_q;
  wire [11:0] output_t;
  wire [15:0] multiplexer_1_out, multiplexer_1_out_2;
  wire [31:0] XY;

  Clock #(.highDuration(1), .lowDuration(1)) clock_1 (.out(CLK));
  Counter #(.width(16), .max('hffff), .ongoal("wrap"), .trigger("rising"), .behavior("old")) counter_1 (
    .count(nHalt), .Q(Cnt), .clk(CLK));  // open: load, D, carry, clr, preset
  // Probe on Cnt
  // Probe on Cnt
  // Probe on 16'hb6
  Comparator #(.width(16), .mode("twosComplement")) comparator_1 (.a(Cnt), .b(16'hb6), .eq(halt));  // open: gt, lt
  ROM #(.addrWidth(16), .dataWidth(17), .Select("high")) rom_1 (
    .addr(Cnt), .data({\外部下按钮 , \外部上按钮 , \内部按钮 , \开关门按钮 , \上下行输入 , \门开启_关闭 , \当前楼层 }));
  ROM #(.addrWidth(16), .dataWidth(12), .Select("high")) rom_2 (.addr(Cnt), .data(output_t));
  not not_1 (nHalt, halt);
  RAM #(.addrWidth(16), .dataWidth(12), .bus("separate"), .Select("low")) ram_1 (
    .addr(Cnt), .din({\开关门请求 [1], \外部下请求 , \开关门请求 [0], \外部上请求 , \内部请求 }), .str(nHalt), .clk(CLK));  // open: data, sel, ld, clr
  not not_2 (NEQ, _passed);
  LED #(.active("true")) \u_测试完成  (.in(halt));
  Counter #(.width(10), .max('h3ff), .ongoal("wrap"), .trigger("rising"), .behavior("old")) counter_2 (
    .count(NEQ), .Q(counter_2_q), .clk(CLK), .clr(halt));  // open: load, D, carry, preset
  and and_1 (and_1_out, ~halt, NEQ);  // AND_Gate
  RAM #(.addrWidth(10), .dataWidth(32), .bus("separate"), .Select("high")) ram_2 (
    .addr(counter_2_q), .din(XY), .str(and_1_out), .clk(CLK));  // open: data, sel, ld, clr
  Pull_Resistor #(.pull(0)) pull_resistor_1 (.node(_passed));
  Comparator #(.width(12), .mode("twosComplement")) comparator_2 (
    .a(output_t), .b({\开关门请求 [1], \外部下请求 , \开关门请求 [0], \外部上请求 , \内部请求 }), .eq(_passed));  // open: gt, lt
  _7_Segment_Display #(.active("true")) u_7_segment_display_1 (
    .g(multiplexer_1_out[15]), .f(multiplexer_1_out[14]), .a(multiplexer_1_out[13]),
    .b(multiplexer_1_out[12]), .e(multiplexer_1_out_2[15]), .d(multiplexer_1_out_2[14]),
    .c(multiplexer_1_out_2[13]), .dp(multiplexer_1_out_2[12]));
  D_Flip_Flop #(.trigger("rising"), .Pre_Clr_Positions("LEGACY"), .NegatePresetClear("false"), .enable("true"), .NewFFLayout("false")) d_ff_1 (
    .clk(CLK), .D(NEQ), .Q(d_ff_1_q), .Qn(d_ff_1_qn), .en(d_ff_1_qn));  // open: preset, reset
  _7_Segment_Display #(.active("true")) u_7_segment_display_2 (
    .g(multiplexer_1_out[7]), .f(multiplexer_1_out[6]), .a(multiplexer_1_out[5]), .b(multiplexer_1_out[4]),
    .e(multiplexer_1_out_2[7]), .d(multiplexer_1_out_2[6]), .c(multiplexer_1_out_2[5]),
    .dp(multiplexer_1_out_2[4]));
  _7_Segment_Display #(.active("true")) u_7_segment_display_3 (
    .g(multiplexer_1_out[11]), .f(multiplexer_1_out[10]), .a(multiplexer_1_out[9]), .b(multiplexer_1_out[8]),
    .e(multiplexer_1_out_2[11]), .d(multiplexer_1_out_2[10]), .c(multiplexer_1_out_2[9]),
    .dp(multiplexer_1_out_2[8]));
  \请求和取消请求  \u_请求和取消请求_1  (
    .\楼层低位 (\当前楼层 [0]), .\内部1楼请求 (\内部按钮 [0]), .\内部1楼请求_2 (\内部请求 [0]), .\外部1楼上 (\外部上按钮 [0]),
    .\_1楼上请求 (\外部上请求 [0]), .\外部2楼下 (\外部下按钮 [0]), .\_2楼下请求 (\外部下请求 [0]), .\楼层高位 (\当前楼层 [1]),
    .\内部2楼请求 (\内部按钮 [1]), .\内部2楼请求_2 (\内部请求 [1]), .\外部2楼上 (\外部上按钮 [1]), .\_2楼上请求 (\外部上请求 [1]),
    .\外部3楼下 (\外部下按钮 [1]), .\_3楼下请求 (\外部下请求 [1]), .\内部3楼请求 (\内部按钮 [2]), .\内部3楼请求_2 (\内部请求 [2]),
    .\上升 (\上下行输入 [0]), .\内部4楼请求 (\内部按钮 [3]), .\内部4楼请求_2 (\内部请求 [3]), .\外部3楼上 (\外部上按钮 [2]),
    .\_3楼上请求 (\外部上请求 [2]), .\外部4楼下 (\外部下按钮 [2]), .\_4楼下请求 (\外部下请求 [2]), .\下降 (\上下行输入 [1]), .\开门 (\门开启_关闭 ),
    .\开门_2 (\开关门按钮 [0]), .\关门 (\开关门按钮 [1]), .\手动开门请求 (\开关门请求 [0]), .\手动关门请求 (\开关门请求 [1]));
  _7_Segment_Display #(.active("true")) u_7_segment_display_4 (
    .g(multiplexer_1_out[3]), .f(multiplexer_1_out[2]), .a(multiplexer_1_out[1]), .b(multiplexer_1_out[0]),
    .e(multiplexer_1_out_2[3]), .d(multiplexer_1_out_2[2]), .c(multiplexer_1_out_2[1]),
    .dp(multiplexer_1_out_2[0]));
  Multiplexer #(.select(1), .width(32), .disabled(0), .enable("true")) multiplexer_1 (
    .in0(32'h8a66ffee), .in1(32'h8a8cef44), .out({multiplexer_1_out_2, multiplexer_1_out}), .sel(d_ff_1_q),
    .en(halt));

  // Other names for the same wires on the sheet: Equal = _passed;
  //   input[16:0] = {\外部下按钮 , \外部上按钮 , \内部按钮 , \开关门按钮 , \上下行输入 , \门开启_关闭 , \当前楼层 }; 开门 = \门开启_关闭 ; tunnel[15:0] = Cnt;
  //   上升 = \上下行输入 [0]; 下降 = \上下行输入 [1]; _1楼 = \内部按钮 [0]; _2楼 = \内部按钮 [1]; _3楼 = \内部按钮 [2]; _4楼 = \内部按钮 [3];
  //   _1楼请求 = \内部请求 [0]; Output[11:0] = {\开关门请求 [1], \外部下请求 , \开关门请求 [0], \外部上请求 , \内部请求 }; _2楼请求 = \内部请求 [1];
  //   _3楼请求 = \内部请求 [2]; _4楼请求 = \内部请求 [3]; _1楼上 = \外部上按钮 [0]; _2楼上 = \外部上按钮 [1]; _3楼上 = \外部上按钮 [2];
  //   _1楼上请求 = \外部上请求 [0]; _2楼上请求 = \外部上请求 [1]; _3楼上请求 = \外部上请求 [2]; _2楼下 = \外部下按钮 [0]; _3楼下 = \外部下按钮 [1];
  //   _4楼下 = \外部下按钮 [2]; _2楼下请求 = \外部下请求 [0]; _3楼下请求 = \外部下请求 [1]; _4楼下请求 = \外部下请求 [2]; 手动开门 = \开关门按钮 [0];
  //   手动关门 = \开关门按钮 [1]; 手动开门请求 = \开关门请求 [0]; 手动关门请求 = \开关门请求 [1]

  // Notes on the sheet:
  //   测试节拍数
  //   contents of rom_1 (hex, n*v repeats v):
  //   0 0 80 0 100 0 0 200 0 400 0 0 800 0 1000 0 2000 0 4000 0 8000 0 10000 0 0 80 0 100 200 0 400 0 800
  //   0 1000 2000 0 4000 0 8000 0 10000 0 0 20 0 4*4 44 4 4*0 80 0 100 0 200 0 400 0 800 0 1000 1000 2000
  //   2000 4000 0 8000 0 10000 10000 0 8 8 8 c c 8 8 8 9 9 d d d 4*9 8 a a e e 4*a b 4*f b b b 3 10003
  //   10003 4*3 2003 3 3 1003 3 3 803 3 3 403 403 3 203 3 103 103 3 83 83 3 3 3 13 13 17 17 13 12 12 16 16
  //   12 12 10 11 15 15 15 11 11 10 14 14 14 10 10 10 0 0 0 1 1 1 5 5 5 1 1 0 2 2 6 6 2 2
  //   contents of rom_2 (hex, n*v repeats v):
  //   0 0 1 1 3 3 3 7 7 f f f 1f 1f 3f 3f 7f 7f 17f 17f 37f 37f 77f 77f 77f 77e 77e 77c 778 778 770 770
  //   760 760 740 700 700 600 600 400 400 0 0 0 80 80 4*0 800 800 4*0 1 1 3 3 7 7 f f 1f 1f 3f 3f 7f 7f
  //   17f 17f 37f 37f 6*77f 7*76e 10*74c 7*708 8*300 6*700 740 740 740 760 760 760 770 770 770 778 778 778
  //   77c 77c 77e 77e 77e 7*77f 5*377 6*173 6*71 12*60 8*40
  //   错误记录X&Y
  //   存储器保存未通过的测试用例
  //   ctrl+K驱动时钟自动测试
endmodule

module \楼层信号合并  (
  input  \内部1楼请求 ,
  input  \_1楼上请求 ,
  input  \_2楼下请求 ,
  input  \内部2楼请求 ,
  input  \_2楼上请求 ,
  input  \_3楼下请求 ,
  input  \内部3楼请求 ,
  input  \_3楼上请求 ,
  input  \_4楼下请求 ,
  input  \内部4楼请求 ,
  output \_1楼有请求 ,
  output \_3楼有请求 ,
  output \_2楼有请求 ,
  output \_4楼有请求 
);

  or or_1 (\_1楼有请求 , \_1楼上请求 , \内部1楼请求 );
  or or_2 (\_4楼有请求 , \内部4楼请求 , \_4楼下请求 );
  or or_3 (\_2楼有请求 , \内部2楼请求 , \_2楼上请求 , \_2楼下请求 );
  or or_4 (\_3楼有请求 , \内部3楼请求 , \_3楼上请求 , \_3楼下请求 );

  // Notes on the sheet:
  //   内部输入
  //   输出
  //   外部输入
endmodule

module \楼层信号合并测试  (
  output [15:0] Cnt,
  output [3:0] \内部请求 ,
  output [2:0] \外部上请求 ,
  output [2:0] \外部下请求 ,
  output \_1楼有请求 ,
  output \_2楼有请求 ,
  output \_3楼有请求 ,
  output \_4楼有请求 ,
  output _passed,
  output halt
);

  wire and_1_out, CLK, d_ff_1_q, d_ff_1_qn, NEQ, nHalt;
  wire [3:0] output_t;
  wire [9:0] counter_2_q;
  wire [15:0] multiplexer_1_out, multiplexer_1_out_2;
  wire [31:0] XY;

  Clock #(.highDuration(1), .lowDuration(1)) clock_1 (.out(CLK));
  Counter #(.width(16), .max('hffff), .ongoal("wrap"), .trigger("rising"), .behavior("old")) counter_1 (
    .count(nHalt), .Q(Cnt), .clk(CLK));  // open: load, D, carry, clr, preset
  // Probe on Cnt
  // Probe on Cnt
  // Probe on 16'h33
  Comparator #(.width(16), .mode("twosComplement")) comparator_1 (.a(Cnt), .b(16'h33), .eq(halt));  // open: gt, lt
  ROM #(.addrWidth(16), .dataWidth(10), .Select("high")) rom_1 (.addr(Cnt), .data({\外部下请求 , \外部上请求 , \内部请求 }));
  ROM #(.addrWidth(16), .dataWidth(4), .Select("high")) rom_2 (.addr(Cnt), .data(output_t));
  not not_1 (nHalt, halt);
  RAM #(.addrWidth(16), .dataWidth(4), .bus("separate"), .Select("low")) ram_1 (
    .addr(Cnt), .din({\_4楼有请求 , \_3楼有请求 , \_2楼有请求 , \_1楼有请求 }), .str(nHalt), .clk(CLK));  // open: data, sel, ld, clr
  not not_2 (NEQ, _passed);
  Counter #(.width(10), .max('h3ff), .ongoal("wrap"), .trigger("rising"), .behavior("old")) counter_2 (
    .count(NEQ), .Q(counter_2_q), .clk(CLK), .clr(halt));  // open: load, D, carry, preset
  Pull_Resistor #(.pull(0)) pull_resistor_1 (.node(_passed));
  Comparator #(.width(4), .mode("twosComplement")) comparator_2 (
    .a(output_t), .b({\_4楼有请求 , \_3楼有请求 , \_2楼有请求 , \_1楼有请求 }), .eq(_passed));  // open: gt, lt
  LED #(.active("true")) \u_测试完成  (.in(halt));
  and and_1 (and_1_out, ~halt, NEQ);  // AND_Gate
  \楼层信号合并  \u_楼层信号合并_1  (
    .\_1楼有请求 (\_1楼有请求 ), .\_1楼上请求 (\外部上请求 [0]), .\_2楼下请求 (\外部下请求 [0]), .\_2楼有请求 (\_2楼有请求 ),
    .\_2楼上请求 (\外部上请求 [1]), .\_3楼下请求 (\外部下请求 [1]), .\_3楼有请求 (\_3楼有请求 ), .\_3楼上请求 (\外部上请求 [2]),
    .\_4楼下请求 (\外部下请求 [2]), .\_4楼有请求 (\_4楼有请求 ), .\内部1楼请求 (\内部请求 [0]), .\内部2楼请求 (\内部请求 [1]),
    .\内部3楼请求 (\内部请求 [2]), .\内部4楼请求 (\内部请求 [3]));
  RAM #(.addrWidth(10), .dataWidth(32), .bus("separate"), .Select("high")) ram_2 (
    .addr(counter_2_q), .din(XY), .str(and_1_out), .clk(CLK));  // open: data, sel, ld, clr
  _7_Segment_Display #(.active("true")) u_7_segment_display_1 (
    .g(multiplexer_1_out[15]), .f(multiplexer_1_out[14]), .a(multiplexer_1_out[13]),
    .b(multiplexer_1_out[12]), .e(multiplexer_1_out_2[15]), .d(multiplexer_1_out_2[14]),
    .c(multiplexer_1_out_2[13]), .dp(multiplexer_1_out_2[12]));
  _7_Segment_Display #(.active("true")) u_7_segment_display_2 (
    .g(multiplexer_1_out[11]), .f(multiplexer_1_out[10]), .a(multiplexer_1_out[9]), .b(multiplexer_1_out[8]),
    .e(multiplexer_1_out_2[11]), .d(multiplexer_1_out_2[10]), .c(multiplexer_1_out_2[9]),
    .dp(multiplexer_1_out_2[8]));
  D_Flip_Flop #(.trigger("rising"), .Pre_Clr_Positions("LEGACY"), .NegatePresetClear("false"), .enable("true"), .NewFFLayout("false")) d_ff_1 (
    .clk(CLK), .D(NEQ), .Q(d_ff_1_q), .Qn(d_ff_1_qn), .en(d_ff_1_qn));  // open: preset, reset
  _7_Segment_Display #(.active("true")) u_7_segment_display_3 (
    .g(multiplexer_1_out[7]), .f(multiplexer_1_out[6]), .a(multiplexer_1_out[5]), .b(multiplexer_1_out[4]),
    .e(multiplexer_1_out_2[7]), .d(multiplexer_1_out_2[6]), .c(multiplexer_1_out_2[5]),
    .dp(multiplexer_1_out_2[4]));
  _7_Segment_Display #(.active("true")) u_7_segment_display_4 (
    .g(multiplexer_1_out[3]), .f(multiplexer_1_out[2]), .a(multiplexer_1_out[1]), .b(multiplexer_1_out[0]),
    .e(multiplexer_1_out_2[3]), .d(multiplexer_1_out_2[2]), .c(multiplexer_1_out_2[1]),
    .dp(multiplexer_1_out_2[0]));
  Multiplexer #(.select(1), .width(32), .disabled(0), .enable("true")) multiplexer_1 (
    .in0(32'h8a66ffee), .in1(32'h8a8cef44), .out({multiplexer_1_out_2, multiplexer_1_out}), .sel(d_ff_1_q),
    .en(halt));

  // Other names for the same wires on the sheet: Equal = _passed;
  //   Output[3:0] = {\_4楼有请求 , \_3楼有请求 , \_2楼有请求 , \_1楼有请求 }; tunnel[15:0] = Cnt;
  //   input[9:0] = {\外部下请求 , \外部上请求 , \内部请求 }; 内部1楼请求 = \内部请求 [0]; 内部2楼请求 = \内部请求 [1]; 内部3楼请求 = \内部请求 [2];
  //   内部4楼请求 = \内部请求 [3]; _1楼上请求 = \外部上请求 [0]; _2楼上请求 = \外部上请求 [1]; _3楼上请求 = \外部上请求 [2]; _2楼下请求 = \外部下请求 [0];
  //   _3楼下请求 = \外部下请求 [1]; _4楼下请求 = \外部下请求 [2]

  // Notes on the sheet:
  //   测试节拍数
  //   contents of rom_1 (hex, n*v repeats v):
  //   0 1 0 2 0 4 8 0 10 0 20 40 0 80 100 0 200 200 200 240 240 340 340 340 360 370 370 3f0 3f0 3f8 3f8
  //   3fc 3fc 3fe 3fe 3ff 3ff 3fe 3fe 3ee 3ee 3ec 3ec 3cc 38c 38c 384 384 184 104 104 4
  //   contents of rom_2 (hex, n*v repeats v):
  //   0 1 0 2 0 4 8 0 1 0 2 4 0 2 4 0 8 8 8 5*c e 14*f 9*e 6 4 4 4
  //   错误记录X&Y
  //   存储器保存未通过的测试用例
  //   ctrl+K驱动时钟自动测试
endmodule

module \电梯上下停判断  (
  input  REQ1,
  input  REQ2,
  input  REQ3,
  input  REQ4,
  input  F0,
  input  F1,
  input  S0,
  input  S1,
  output N0,
  output N1
);

  wire and_1_out, and_2_out, and_3_out, and_4_out, and_5_out, and_6_out, and_7_out, and_8_out, and_9_out,
       and_10_out, and_11_out, and_12_out, and_13_out, and_14_out, and_15_out, and_16_out, and_17_out,
       and_18_out, not_1_out, not_2_out, not_3_out, not_4_out, not_5_out, not_6_out, not_7_out, not_8_out,
       not_9_out, not_10_out, not_11_out, not_12_out, not_13_out, not_14_out, not_15_out, not_16_out,
       not_17_out, not_18_out, not_19_out, not_20_out, not_21_out, not_22_out, not_23_out, not_24_out,
       not_25_out, not_26_out, not_27_out, not_28_out, not_29_out, not_30_out, not_31_out, not_32_out,
       not_33_out, not_34_out, not_35_out, not_36_out, not_37_out, not_38_out;

  not not_1 (not_1_out, F0);
  not not_2 (not_2_out, F1);
  not not_3 (not_3_out, F0);
  not not_4 (not_4_out, F1);
  not not_5 (not_5_out, F0);
  not not_6 (not_6_out, F1);
  not not_7 (not_7_out, S1);
  not not_8 (not_8_out, F1);
  not not_9 (not_9_out, S1);
  not not_10 (not_10_out, F1);
  not not_11 (not_11_out, S0);
  not not_12 (not_12_out, REQ1);
  not not_13 (not_13_out, F1);
  not not_14 (not_14_out, S0);
  not not_15 (not_15_out, REQ1);
  not not_16 (not_16_out, F1);
  not not_17 (not_17_out, S1);
  not not_18 (not_18_out, F0);
  not not_19 (not_19_out, S0);
  not not_20 (not_20_out, REQ1);
  not not_21 (not_21_out, REQ2);
  not not_22 (not_22_out, F0);
  not not_23 (not_23_out, S1);
  not not_24 (not_24_out, REQ3);
  not not_25 (not_25_out, REQ4);
  not not_26 (not_26_out, F1);
  not not_27 (not_27_out, S0);
  not not_28 (not_28_out, F1);
  not not_29 (not_29_out, S1);
  not not_30 (not_30_out, REQ4);
  not not_31 (not_31_out, F0);
  not not_32 (not_32_out, S1);
  not not_33 (not_33_out, REQ4);
  not not_34 (not_34_out, F0);
  not not_35 (not_35_out, S0);
  not not_36 (not_36_out, F0);
  not not_37 (not_37_out, S0);
  not not_38 (not_38_out, F0);
  and and_1 (and_1_out, REQ2, not_1_out, not_2_out);
  and and_2 (and_2_out, REQ3, not_3_out, not_4_out);
  and and_3 (and_3_out, REQ4, not_5_out, not_6_out);
  and and_4 (and_4_out, not_7_out, REQ4, F0, not_8_out);
  and and_5 (and_5_out, not_9_out, REQ3, F0, not_10_out);
  and and_6 (and_6_out, S1, not_11_out, not_12_out, REQ3, F0, not_13_out);
  and and_7 (and_7_out, S1, not_14_out, not_15_out, REQ4, F0, not_16_out);
  and and_8 (and_8_out, not_17_out, REQ4, not_18_out, F1);
  and and_9 (and_9_out, S1, not_19_out, not_20_out, not_21_out, REQ4, not_22_out, F1);
  and and_10 (and_10_out, not_23_out, REQ1, not_24_out, not_25_out, F0, not_26_out);
  and and_11 (and_11_out, S1, not_27_out, REQ1, F0, not_28_out);
  and and_12 (and_12_out, not_29_out, REQ1, not_30_out, not_31_out, F1);
  and and_13 (and_13_out, not_32_out, REQ2, not_33_out, not_34_out, F1);
  and and_14 (and_14_out, S1, not_35_out, REQ1, not_36_out, F1);
  and and_15 (and_15_out, S1, not_37_out, REQ2, not_38_out, F1);
  and and_16 (and_16_out, REQ3, F0, F1);
  and and_17 (and_17_out, REQ2, F0, F1);
  and and_18 (and_18_out, REQ1, F0, F1);
  or or_1 (N0, and_1_out, and_2_out, and_3_out, and_4_out, and_5_out, and_6_out, and_7_out, and_8_out, and_9_out);
  or or_2 (N1, and_10_out, and_11_out, and_12_out, and_13_out, and_14_out, and_15_out, and_16_out, and_17_out, and_18_out);
endmodule

module \电梯上下停判断测试  (
  output [15:0] Cnt,
  output [1:0] \当前楼层 ,
  output REQ1,
  output REQ2,
  output REQ3,
  output REQ4,
  output F0,
  output F1,
  output S0,
  output S1,
  output N0,
  output N1,
  output _passed,
  output halt
);

  wire and_1_out, CLK, d_ff_1_q, d_ff_1_qn, NEQ, nHalt;
  wire [1:0] output_t;
  wire [9:0] counter_2_q;
  wire [15:0] multiplexer_1_out, multiplexer_1_out_2;
  wire [31:0] XY;

  Clock #(.highDuration(1), .lowDuration(1)) clock_1 (.out(CLK));
  Counter #(.width(16), .max('hffff), .ongoal("wrap"), .trigger("rising"), .behavior("old")) counter_1 (
    .count(nHalt), .Q(Cnt), .clk(CLK));  // open: load, D, carry, clr, preset
  // Probe on Cnt
  // Probe on Cnt
  // Probe on 16'hff
  not not_1 (NEQ, _passed);
  Counter #(.width(10), .max('h3ff), .ongoal("wrap"), .trigger("rising"), .behavior("old")) counter_2 (
    .count(NEQ), .Q(counter_2_q), .clk(CLK), .clr(halt));  // open: load, D, carry, preset
  Comparator #(.width(16), .mode("twosComplement")) comparator_1 (.a(Cnt), .b(16'hff), .eq(halt));  // open: gt, lt
  LED #(.active("true")) \u_测试完成  (.in(halt));
  and and_1 (and_1_out, ~halt, NEQ);  // AND_Gate
  ROM #(.addrWidth(16), .dataWidth(8), .Select("high")) rom_1 (
    .addr(Cnt), .data({S1, S0, F1, F0, REQ4, REQ3, REQ2, REQ1}));
  ROM #(.addrWidth(16), .dataWidth(2), .Select("high")) rom_2 (.addr(Cnt), .data(output_t));
  not not_2 (nHalt, halt);
  RAM #(.addrWidth(16), .dataWidth(2), .bus("separate"), .Select("low")) ram_1 (
    .addr(Cnt), .din({N1, N0}), .str(nHalt), .clk(CLK));  // open: data, sel, ld, clr
  RAM #(.addrWidth(10), .dataWidth(32), .bus("separate"), .Select("high")) ram_2 (
    .addr(counter_2_q), .din(XY), .str(and_1_out), .clk(CLK));  // open: data, sel, ld, clr
  _7_Segment_Display #(.active("true")) u_7_segment_display_1 (
    .g(multiplexer_1_out[11]), .f(multiplexer_1_out[10]), .a(multiplexer_1_out[9]), .b(multiplexer_1_out[8]),
    .e(multiplexer_1_out_2[11]), .d(multiplexer_1_out_2[10]), .c(multiplexer_1_out_2[9]),
    .dp(multiplexer_1_out_2[8]));
  _7_Segment_Display #(.active("true")) u_7_segment_display_2 (
    .g(multiplexer_1_out[15]), .f(multiplexer_1_out[14]), .a(multiplexer_1_out[13]),
    .b(multiplexer_1_out[12]), .e(multiplexer_1_out_2[15]), .d(multiplexer_1_out_2[14]),
    .c(multiplexer_1_out_2[13]), .dp(multiplexer_1_out_2[12]));
  D_Flip_Flop #(.trigger("rising"), .Pre_Clr_Positions("LEGACY"), .NegatePresetClear("false"), .enable("true"), .NewFFLayout("false")) d_ff_1 (
    .clk(CLK), .D(NEQ), .Q(d_ff_1_q), .Qn(d_ff_1_qn), .en(d_ff_1_qn));  // open: preset, reset
  _7_Segment_Display #(.active("true")) u_7_segment_display_3 (
    .g(multiplexer_1_out[7]), .f(multiplexer_1_out[6]), .a(multiplexer_1_out[5]), .b(multiplexer_1_out[4]),
    .e(multiplexer_1_out_2[7]), .d(multiplexer_1_out_2[6]), .c(multiplexer_1_out_2[5]),
    .dp(multiplexer_1_out_2[4]));
  _7_Segment_Display #(.active("true")) u_7_segment_display_4 (
    .g(multiplexer_1_out[3]), .f(multiplexer_1_out[2]), .a(multiplexer_1_out[1]), .b(multiplexer_1_out[0]),
    .e(multiplexer_1_out_2[3]), .d(multiplexer_1_out_2[2]), .c(multiplexer_1_out_2[1]),
    .dp(multiplexer_1_out_2[0]));
  Pull_Resistor #(.pull(0)) pull_resistor_1 (.node(_passed));
  Comparator #(.width(2), .mode("twosComplement")) comparator_2 (
    .a(output_t), .b({N1, N0}), .eq(_passed));  // open: gt, lt
  // 电梯上下停判断 电梯上下停判断_1: pin names not known; wires that end beside it: REQ1, REQ2, REQ3, REQ4, F0, F1, S0, N0, N1
  Multiplexer #(.select(1), .width(32), .disabled(0), .enable("true")) multiplexer_1 (
    .in0(32'h8a66ffee), .in1(32'h8a8cef44), .out({multiplexer_1_out_2, multiplexer_1_out}), .sel(d_ff_1_q),
    .en(halt));

  assign \当前楼层  = {REQ2, REQ1};

  // Other names for the same wires on the sheet: Equal = _passed;
  //   input[7:0] = {S1, S0, F1, F0, REQ4, REQ3, REQ2, REQ1}; Output[1:0] = {N1, N0}; tunnel[15:0] = Cnt

  // Notes on the sheet:
  //   测试节拍数
  //   contents of rom_1 (hex, n*v repeats v):
  //   0 1 2 3 4 5 6 7 8 9 a b c d e f 10 11 12 13 14 15 16 17 18 19 1a 1b 1c 1d 1e 1f 20 21 22 23 24 25 26
  //   27 28 29 2a 2b 2c 2d 2e 2f 30 31 32 33 34 35 36 37 38 39 3a 3b 3c 3d 3e 3f 40 41 42 43 44 45 46 47
  //   48 49 4a 4b 4c 4d 4e 4f 50 51 52 53 54 55 56 57 58 59 5a 5b 5c 5d 5e 5f 60 61 62 63 64 65 66 67 68
  //   69 6a 6b 6c 6d 6e 6f 70 71 72 73 74 75 76 77 78 79 7a 7b 7c 7d 7e 7f 80 81 82 83 84 85 86 87 88 89
  //   8a 8b 8c 8d 8e 8f 90 91 92 93 94 95 96 97 98 99 9a 9b 9c 9d 9e 9f a0 a1 a2 a3 a4 a5 a6 a7 a8 a9 aa
  //   ab ac ad ae af b0 b1 b2 b3 b4 b5 b6 b7 b8 b9 ba bb bc bd be bf c0 c1 c2 c3 c4 c5 c6 c7 c8 c9 ca cb
  //   cc cd ce cf d0 d1 d2 d3 d4 d5 d6 d7 d8 d9 da db dc dd de df e0 e1 e2 e3 e4 e5 e6 e7 e8 e9 ea eb ec
  //   ed ee ef f0 f1 f2 f3 f4 f5 f6 f7 f8 f9 fa fb fc fd fe ff
  //   contents of rom_2 (hex, n*v repeats v):
  //   0 0 14*1 0 2 0 2 12*1 0 2 2 2 0 2 2 2 8*1 0 7*2 0 7*2 0 0 14*1 0 2 0 2 12*1 0 2 2 2 0 2 2 2 8*1 0
  //   7*2 0 7*2 0 0 14*1 0 2 0 2 1 2 1 2 1 2 1 2 1 2 1 2 0 2 2 2 0 2 2 2 1 2 2 2 1 2 2 2 0 7*2 0 7*2 0 0
  //   14*1 33*0 7*2 0 7*2
  //   错误记录X&Y
  //   存储器保存未通过的测试用例
  //   ctrl+K驱动时钟自动测试
endmodule

module \电梯上下停状态转移  (
  input  \_1楼有请求 ,
  input  \_2楼有请求 ,
  input  \楼层低位 ,
  input  \_3楼有请求 ,
  input  \楼层高位 ,
  input  \_4楼有请求 ,
  output \上升 ,
  output \下降 
);

  wire CLK, d_ff_1_q, d_ff_1_qn, d_ff_2_q, d_ff_2_qn, \电梯上下停判断_1_n0 , \电梯上下停判断_1_n1 ;

  \电梯上下停判断  \u_电梯上下停判断_1  (
    .REQ1(\_1楼有请求 ), .REQ2(\_2楼有请求 ), .REQ3(\_3楼有请求 ), .REQ4(\_4楼有请求 ), .F0(\楼层低位 ), .F1(\楼层高位 ),
    .S0(d_ff_1_q), .N0(\电梯上下停判断_1_n0 ), .S1(d_ff_2_q), .N1(\电梯上下停判断_1_n1 ));
  Clock #(.highDuration(1), .lowDuration(1)) clock_1 (.out(CLK));
  D_Flip_Flop #(.trigger("rising"), .Pre_Clr_Positions("ABOVE_BELOW"), .NegatePresetClear("false"), .enable("false"), .NewFFLayout("true")) d_ff_1 (
    .clk(CLK), .D(\电梯上下停判断_1_n0 ), .Q(d_ff_1_q), .Qn(d_ff_1_qn));  // open: preset, reset
  D_Flip_Flop #(.trigger("rising"), .Pre_Clr_Positions("ABOVE_BELOW"), .NegatePresetClear("false"), .enable("false"), .NewFFLayout("true")) d_ff_2 (
    .clk(CLK), .D(\电梯上下停判断_1_n1 ), .Q(d_ff_2_q), .Qn(d_ff_2_qn));  // open: preset, reset
  // Probe on {\楼层高位 , \楼层低位 }
  and and_1 (\上升 , d_ff_1_q, d_ff_2_qn);
  and and_2 (\下降 , d_ff_1_qn, d_ff_2_q);

  // Other names for the same wires on the sheet: 当前楼层[1:0] = {\楼层高位 , \楼层低位 }

  // Notes on the sheet:
  //   输入
  //   输出
endmodule

module \电梯上下停状态转移测试  (
  output [15:0] Cnt,
  output [1:0] \当前楼层 ,
  output \_1楼有请求 ,
  output \_2楼有请求 ,
  output \_3楼有请求 ,
  output \_4楼有请求 ,
  output [1:0] \上升_下降 ,
  output _passed,
  output halt
);

  wire and_1_out, CLK, d_ff_1_q, d_ff_1_qn, NEQ, nHalt;
  wire [1:0] output_t;
  wire [9:0] counter_2_q;
  wire [15:0] multiplexer_1_out, multiplexer_1_out_2;
  wire [31:0] XY;

  Clock #(.highDuration(1), .lowDuration(1)) clock_1 (.out(CLK));
  Counter #(.width(16), .max('hffff), .ongoal("wrap"), .trigger("rising"), .behavior("old")) counter_1 (
    .count(nHalt), .Q(Cnt), .clk(CLK));  // open: load, D, carry, clr, preset
  // Probe on Cnt
  // Probe on Cnt
  // Probe on 16'h65
  Comparator #(.width(16), .mode("twosComplement")) comparator_1 (.a(Cnt), .b(16'h65), .eq(halt));  // open: gt, lt
  ROM #(.addrWidth(16), .dataWidth(6), .Select("high")) rom_1 (
    .addr(Cnt), .data({\_4楼有请求 , \_3楼有请求 , \_2楼有请求 , \_1楼有请求 , \当前楼层 }));
  ROM #(.addrWidth(16), .dataWidth(2), .Select("high")) rom_2 (.addr(Cnt), .data(output_t));
  not not_1 (nHalt, halt);
  RAM #(.addrWidth(16), .dataWidth(2), .bus("separate"), .Select("low")) ram_1 (
    .addr(Cnt), .din(\上升_下降 ), .str(nHalt), .clk(CLK));  // open: data, sel, ld, clr
  \电梯上下停状态转移  \u_电梯上下停状态转移_1  (
    .\_1楼有请求 (\_1楼有请求 ), .\_2楼有请求 (\_2楼有请求 ), .\楼层低位 (\当前楼层 [0]), .\_3楼有请求 (\_3楼有请求 ), .\楼层高位 (\当前楼层 [1]),
    .\_4楼有请求 (\_4楼有请求 ), .\上升 (\上升_下降 [0]), .\下降 (\上升_下降 [1]));
  not not_2 (NEQ, _passed);
  LED #(.active("true")) \u_测试完成  (.in(halt));
  Counter #(.width(10), .max('h3ff), .ongoal("wrap"), .trigger("rising"), .behavior("old")) counter_2 (
    .count(NEQ), .Q(counter_2_q), .clk(CLK), .clr(halt));  // open: load, D, carry, preset
  Pull_Resistor #(.pull(0)) pull_resistor_1 (.node(_passed));
  Comparator #(.width(2), .mode("twosComplement")) comparator_2 (
    .a(output_t), .b(\上升_下降 ), .eq(_passed));  // open: gt, lt
  and and_1 (and_1_out, ~halt, NEQ);  // AND_Gate
  RAM #(.addrWidth(10), .dataWidth(32), .bus("separate"), .Select("high")) ram_2 (
    .addr(counter_2_q), .din(XY), .str(and_1_out), .clk(CLK));  // open: data, sel, ld, clr
  _7_Segment_Display #(.active("true")) u_7_segment_display_1 (
    .g(multiplexer_1_out[15]), .f(multiplexer_1_out[14]), .a(multiplexer_1_out[13]),
    .b(multiplexer_1_out[12]), .e(multiplexer_1_out_2[15]), .d(multiplexer_1_out_2[14]),
    .c(multiplexer_1_out_2[13]), .dp(multiplexer_1_out_2[12]));
  _7_Segment_Display #(.active("true")) u_7_segment_display_2 (
    .g(multiplexer_1_out[7]), .f(multiplexer_1_out[6]), .a(multiplexer_1_out[5]), .b(multiplexer_1_out[4]),
    .e(multiplexer_1_out_2[7]), .d(multiplexer_1_out_2[6]), .c(multiplexer_1_out_2[5]),
    .dp(multiplexer_1_out_2[4]));
  _7_Segment_Display #(.active("true")) u_7_segment_display_3 (
    .g(multiplexer_1_out[11]), .f(multiplexer_1_out[10]), .a(multiplexer_1_out[9]), .b(multiplexer_1_out[8]),
    .e(multiplexer_1_out_2[11]), .d(multiplexer_1_out_2[10]), .c(multiplexer_1_out_2[9]),
    .dp(multiplexer_1_out_2[8]));
  D_Flip_Flop #(.trigger("rising"), .Pre_Clr_Positions("LEGACY"), .NegatePresetClear("false"), .enable("true"), .NewFFLayout("false")) d_ff_1 (
    .clk(CLK), .D(NEQ), .Q(d_ff_1_q), .Qn(d_ff_1_qn), .en(d_ff_1_qn));  // open: preset, reset
  _7_Segment_Display #(.active("true")) u_7_segment_display_4 (
    .g(multiplexer_1_out[3]), .f(multiplexer_1_out[2]), .a(multiplexer_1_out[1]), .b(multiplexer_1_out[0]),
    .e(multiplexer_1_out_2[3]), .d(multiplexer_1_out_2[2]), .c(multiplexer_1_out_2[1]),
    .dp(multiplexer_1_out_2[0]));
  Multiplexer #(.select(1), .width(32), .disabled(0), .enable("true")) multiplexer_1 (
    .in0(32'h8a66ffee), .in1(32'h8a8cef44), .out({multiplexer_1_out_2, multiplexer_1_out}), .sel(d_ff_1_q),
    .en(halt));

  // Other names for the same wires on the sheet: Equal = _passed;
  //   input[5:0] = {\_4楼有请求 , \_3楼有请求 , \_2楼有请求 , \_1楼有请求 , \当前楼层 }; tunnel[15:0] = Cnt; Output[1:0] = \上升_下降 ;
  //   上升 = \上升_下降 [0]; 下降 = \上升_下降 [1]

  // Notes on the sheet:
  //   测试节拍数
  //   contents of rom_1 (hex, n*v repeats v):
  //   0 4 4 0 8 8 8 10 10 10 20 20 20 0 18 18 18 4*28 18 30 30 0 0 1 1 5 5 1 9 1 11 11 11 21 21 21 1 31 31
  //   1 0 2 2 6 2 a a 2 e e 2 22 22 22 2 3 3 7 7 7 3 b b 13 13 3 1b 1b b f f f 17 17 17 1f 1f 1f 3f 3f 1f
  //   1f 1f f f e e 4*2e e e d d 2d 25 25 5 1
  //   contents of rom_2 (hex, n*v repeats v):
  //   5*0 9*1 0 10*1 4*0 2 2 0 0 0 6*1 0 1 1 4*0 2 0 2 2 0 2 2 0 1 1 1 0 0 0 2 2 2 0 4*2 0 33*2
  //   错误记录X&Y
  //   存储器保存未通过的测试用例
  //   ctrl+K驱动时钟自动测试
endmodule

module \开门请求计算  (
  input  \_1楼上请求 ,
  input  \内部1楼请求 ,
  input  \楼层低位 ,
  input  \_2楼上请求 ,
  input  \内部2楼请求 ,
  input  \楼层高位 ,
  input  \_3楼上请求 ,
  input  \内部3楼请求 ,
  input  \_2楼下请求 ,
  input  \内部4楼请求 ,
  input  \上升 ,
  input  \_3楼下请求 ,
  input  \下降 ,
  input  \_4楼下请求 ,
  output out_15
);

  wire \_1层开门 , \_2层开门 , \_3层开门 , \_4层开门 , and_1_out, and_2_out, and_3_out, and_4_out, and_5_out, and_6_out,
       and_7_out, and_8_out, not_1_out, not_2_out, not_3_out, not_4_out, not_5_out, not_6_out, not_7_out,
       not_8_out;

  and and_1 (and_1_out, \_2楼上请求 , not_1_out);
  not not_1 (not_1_out, \下降 );
  and and_2 (and_2_out, \_2楼下请求 , not_2_out);
  not not_2 (not_2_out, \上升 );
  or or_1 (\_1层开门 , \内部1楼请求 , \_1楼上请求 );
  or or_2 (\_2层开门 , and_1_out, \内部2楼请求 , and_2_out);
  and and_3 (and_3_out, \_1层开门 , not_3_out, not_4_out);
  not not_3 (not_3_out, \楼层低位 );
  not not_4 (not_4_out, \楼层高位 );
  and and_4 (and_4_out, \_2层开门 , \楼层低位 , not_5_out);
  not not_5 (not_5_out, \楼层高位 );
  not not_6 (not_6_out, \楼层低位 );
  and and_5 (and_5_out, \_3层开门 , not_6_out, \楼层高位 );
  and and_6 (and_6_out, \_4层开门 , \楼层低位 , \楼层高位 );
  or or_3 (out_15, and_3_out, and_4_out, and_5_out, and_6_out);
  not not_7 (not_7_out, \下降 );
  not not_8 (not_8_out, \上升 );
  and and_7 (and_7_out, \_3楼上请求 , not_7_out);
  or or_4 (\_3层开门 , and_7_out, \内部3楼请求 , and_8_out);
  and and_8 (and_8_out, \_3楼下请求 , not_8_out);
  // Probe on {\楼层高位 , \楼层低位 }
  or or_5 (\_4层开门 , \内部4楼请求 , \_4楼下请求 );

  // Other names for the same wires on the sheet: 当前楼层[1:0] = {\楼层高位 , \楼层低位 }; 请求开门 = out_15

  // Notes on the sheet:
  //   内部输入
  //   外部输入
  //   其他输入
endmodule

module \开门请求计算测试  (
  output [15:0] Cnt,
  output [1:0] \当前楼层 ,
  output [3:0] \内部请求 ,
  output [2:0] \外部上请求 ,
  output [2:0] \外部下请求 ,
  output [1:0] \上升_下降 ,
  output \开门_关门 ,
  output _passed,
  output halt
);

  wire and_1_out, CLK, d_ff_1_q, d_ff_1_qn, NEQ, nHalt, output_t;
  wire [9:0] counter_2_q;
  wire [15:0] multiplexer_1_out, multiplexer_1_out_2;
  wire [31:0] XY;

  Clock #(.highDuration(1), .lowDuration(1)) clock_1 (.out(CLK));
  Counter #(.width(16), .max('hffff), .ongoal("wrap"), .trigger("rising"), .behavior("old")) counter_1 (
    .count(nHalt), .Q(Cnt), .clk(CLK));  // open: load, D, carry, clr, preset
  // Probe on Cnt
  // Probe on Cnt
  // Probe on 16'h600
  Comparator #(.width(16), .mode("twosComplement")) comparator_1 (.a(Cnt), .b(16'h600), .eq(halt));  // open: gt, lt
  ROM #(.addrWidth(16), .dataWidth(14), .Select("high")) rom_1 (
    .addr(Cnt),
    .data({\外部下请求 [0], \内部请求 [1], \外部上请求 [2], \上升_下降 , \当前楼层 , \外部下请求 [2:1], \外部上请求 [1:0], \内部请求 [3:2], \内部请求 [0]}));
  ROM #(.addrWidth(16), .dataWidth(1), .Select("high")) rom_2 (.addr(Cnt), .data(output_t));
  not not_1 (nHalt, halt);
  RAM #(.addrWidth(16), .dataWidth(1), .bus("separate"), .Select("low")) ram_1 (
    .addr(Cnt), .din(\开门_关门 ), .str(nHalt), .clk(CLK));  // open: data, sel, ld, clr
  not not_2 (NEQ, _passed);
  LED #(.active("true")) \u_测试完成  (.in(halt));
  Counter #(.width(10), .max('h3ff), .ongoal("wrap"), .trigger("rising"), .behavior("old")) counter_2 (
    .count(NEQ), .Q(counter_2_q), .clk(CLK), .clr(halt));  // open: load, D, carry, preset
  Pull_Resistor #(.pull(0)) pull_resistor_1 (.node(_passed));
  Comparator #(.width(1), .mode("twosComplement")) comparator_2 (
    .a(output_t), .b(\开门_关门 ), .eq(_passed));  // open: gt, lt
  \开门请求计算  \u_开门请求计算_1  (
    .\楼层低位 (\当前楼层 [0]), .\楼层高位 (\当前楼层 [1]), .\上升 (\上升_下降 [0]), .\下降 (\上升_下降 [1]), .out_15(\开门_关门 ),
    .\内部1楼请求 (\内部请求 [0]), .\_1楼上请求 (\外部上请求 [0]), .\_2楼下请求 (\外部下请求 [0]), .\内部2楼请求 (\内部请求 [1]),
    .\_2楼上请求 (\外部上请求 [1]), .\_3楼下请求 (\外部下请求 [1]), .\内部3楼请求 (\内部请求 [2]), .\_3楼上请求 (\外部上请求 [2]),
    .\_4楼下请求 (\外部下请求 [2]), .\内部4楼请求 (\内部请求 [3]));
  and and_1 (and_1_out, ~halt, NEQ);  // AND_Gate
  RAM #(.addrWidth(10), .dataWidth(32), .bus("separate"), .Select("high")) ram_2 (
    .addr(counter_2_q), .din(XY), .str(and_1_out), .clk(CLK));  // open: data, sel, ld, clr
  _7_Segment_Display #(.active("true")) u_7_segment_display_1 (
    .g(multiplexer_1_out[15]), .f(multiplexer_1_out[14]), .a(multiplexer_1_out[13]),
    .b(multiplexer_1_out[12]), .e(multiplexer_1_out_2[15]), .d(multiplexer_1_out_2[14]),
    .c(multiplexer_1_out_2[13]), .dp(multiplexer_1_out_2[12]));
  D_Flip_Flop #(.trigger("rising"), .Pre_Clr_Positions("LEGACY"), .NegatePresetClear("false"), .enable("true"), .NewFFLayout("false")) d_ff_1 (
    .clk(CLK), .D(NEQ), .Q(d_ff_1_q), .Qn(d_ff_1_qn), .en(d_ff_1_qn));  // open: preset, reset
  _7_Segment_Display #(.active("true")) u_7_segment_display_2 (
    .g(multiplexer_1_out[11]), .f(multiplexer_1_out[10]), .a(multiplexer_1_out[9]), .b(multiplexer_1_out[8]),
    .e(multiplexer_1_out_2[11]), .d(multiplexer_1_out_2[10]), .c(multiplexer_1_out_2[9]),
    .dp(multiplexer_1_out_2[8]));
  _7_Segment_Display #(.active("true")) u_7_segment_display_3 (
    .g(multiplexer_1_out[7]), .f(multiplexer_1_out[6]), .a(multiplexer_1_out[5]), .b(multiplexer_1_out[4]),
    .e(multiplexer_1_out_2[7]), .d(multiplexer_1_out_2[6]), .c(multiplexer_1_out_2[5]),
    .dp(multiplexer_1_out_2[4]));
  _7_Segment_Display #(.active("true")) u_7_segment_display_4 (
    .g(multiplexer_1_out[3]), .f(multiplexer_1_out[2]), .a(multiplexer_1_out[1]), .b(multiplexer_1_out[0]),
    .e(multiplexer_1_out_2[3]), .d(multiplexer_1_out_2[2]), .c(multiplexer_1_out_2[1]),
    .dp(multiplexer_1_out_2[0]));
  Multiplexer #(.select(1), .width(32), .disabled(0), .enable("true")) multiplexer_1 (
    .in0(32'h8a66ffee), .in1(32'h8a8cef44), .out({multiplexer_1_out_2, multiplexer_1_out}), .sel(d_ff_1_q),
    .en(halt));

  // Other names for the same wires on the sheet: Equal = _passed;
  //   input[13:0] = {\外部下请求 [0], \内部请求 [1], \外部上请求 [2], \上升_下降 , \当前楼层 , \外部下请求 [2:1], \外部上请求 [1:0], \内部请求 [3:2], \内部请求 [0]};
  //   Output = \开门_关门 ; tunnel[15:0] = Cnt; 上升 = \上升_下降 [0]; 下降 = \上升_下降 [1]; _1楼请求 = \内部请求 [0]; _2楼请求 = \内部请求 [1];
  //   _3楼请求 = \内部请求 [2]; _4楼请求 = \内部请求 [3]; _1楼上请求 = \外部上请求 [0]; _2楼上请求 = \外部上请求 [1]; _3楼上请求 = \外部上请求 [2];
  //   _2楼下请求 = \外部下请求 [0]; _3楼下请求 = \外部下请求 [1]; _4楼下请求 = \外部下请求 [2]

  // Notes on the sheet:
  //   测试节拍数
  //   contents of rom_1 (hex, n*v repeats v):
  //   0 1 2 3 4 5 6 7 8 9 a b c d e f 10 11 12 13 14 15 16 17 18 19 1a 1b 1c 1d 1e 1f 20 21 22 23 24 25 26
  //   27 28 29 2a 2b 2c 2d 2e 2f 30 31 32 33 34 35 36 37 38 39 3a 3b 3c 3d 3e 3f 40 41 42 43 44 45 46 47
  //   48 49 4a 4b 4c 4d 4e 4f 50 51 52 53 54 55 56 57 58 59 5a 5b 5c 5d 5e 5f 60 61 62 63 64 65 66 67 68
  //   69 6a 6b 6c 6d 6e 6f 70 71 72 73 74 75 76 77 78 79 7a 7b 7c 7d 7e 7f 80 81 82 83 84 85 86 87 88 89
  //   8a 8b 8c 8d 8e 8f 90 91 92 93 94 95 96 97 98 99 9a 9b 9c 9d 9e 9f a0 a1 a2 a3 a4 a5 a6 a7 a8 a9 aa
  //   ab ac ad ae af b0 b1 b2 b3 b4 b5 b6 b7 b8 b9 ba bb bc bd be bf c0 c1 c2 c3 c4 c5 c6 c7 c8 c9 ca cb
  //   cc cd ce cf d0 d1 d2 d3 d4 d5 d6 d7 d8 d9 da db dc dd de df e0 e1 e2 e3 e4 e5 e6 e7 e8 e9 ea eb ec
  //   ed ee ef f0 f1 f2 f3 f4 f5 f6 f7 f8 f9 fa fb fc fd fe ff 100 101 102 103 104 105 106 107 108 109 10a
  //   10b 10c 10d 10e 10f 110 111 112 113 114 115 116 117 118 119 11a 11b 11c 11d 11e 11f 120 121 122 123
  //   124 125 126 127 128 129 12a 12b 12c 12d 12e 12f 130 131 132 133 134 135 136 137 138 139 13a 13b 13c
  //   13d 13e 13f 140 141 142 143 144 145 146 147 148 149 14a 14b 14c 14d 14e 14f 150 151 152 153 154 155
  //   156 157 158 159 15a 15b 15c 15d 15e 15f 160 161 162 163 164 165 166 167 168 169 16a 16b 16c 16d 16e
  //   16f 170 171 172 173 174 175 176 177 178 179 17a 17b 17c 17d 17e 17f 180 181 182 183 184 185 186 187
  //   188 189 18a 18b 18c 18d 18e 18f 190 191 192 193 194 195 196 197 198 199 19a 19b 19c 19d 19e 19f 1a0
  //   1a1 1a2 1a3 1a4 1a5 1a6 1a7 1a8 1a9 1aa 1ab 1ac 1ad 1ae 1af 1b0 1b1 1b2 1b3 1b4 1b5 1b6 1b7 1b8 1b9
  //   1ba 1bb 1bc 1bd 1be 1bf 1c0 1c1 1c2 1c3 1c4 1c5 1c6 1c7 1c8 1c9 1ca 1cb 1cc 1cd 1ce 1cf 1d0 1d1 1d2
  //   1d3 1d4 1d5 1d6 1d7 1d8 1d9 1da 1db 1dc 1dd 1de 1df 1e0 1e1 1e2 1e3 1e4 1e5 1e6 1e7 1e8 1e9 1ea 1eb
  //   1ec 1ed 1ee 1ef 1f0 1f1 1f2 1f3 1f4 1f5 1f6 1f7 1f8 1f9 1fa 1fb 1fc 1fd 1fe 1ff 200 201 202 203 204
  //   205 206 207 208 209 20a 20b 20c 20d 20e 20f 210 211 212 213 214 215 216 217 218 219 21a 21b 21c 21d
  //   21e 21f 220 221 222 223 224 225 226 227 228 229 22a 22b 22c 22d 22e 22f 230 231 232 233 234 235 236
  //   237 238 239 23a 23b 23c 23d 23e 23f 240 241 242 243 244 245 246 247 248 249 24a 24b 24c 24d 24e 24f
  //   250 251 252 253 254 255 256 257 258 259 25a 25b 25c 25d 25e 25f 260 261 262 263 264 265 266 267 268
  //   269 26a 26b 26c 26d 26e 26f 270 271 272 273 274 275 276 277 278 279 27a 27b 27c 27d 27e 27f 280 281
  //   282 283 284 285 286 287 288 289 28a 28b 28c 28d 28e 28f 290 291 292 293 294 295 296 297 298 299 29a
  //   29b 29c 29d 29e 29f 2a0 2a1 2a2 2a3 2a4 2a5 2a6 2a7 2a8 2a9 2aa 2ab 2ac 2ad 2ae 2af 2b0 2b1 2b2 2b3
  //   2b4 2b5 2b6 2b7 2b8 2b9 2ba 2bb 2bc 2bd 2be 2bf 2c0 2c1 2c2 2c3 2c4 2c5 2c6 2c7 2c8 2c9 2ca 2cb 2cc
  //   2cd 2ce 2cf 2d0 2d1 2d2 2d3 2d4 2d5 2d6 2d7 2d8 2d9 2da 2db 2dc 2dd 2de 2df 2e0 2e1 2e2 2e3 2e4 2e5
  //   2e6 2e7 2e8 2e9 2ea 2eb 2ec 2ed 2ee 2ef 2f0 2f1 2f2 2f3 2f4 2f5 2f6 2f7 2f8 2f9 2fa 2fb 2fc 2fd 2fe
  //   2ff 300 301 302 303 304 305 306 307 308 309 30a 30b 30c 30d 30e 30f 310 311 312 313 314 315 316 317
  //   318 319 31a 31b 31c 31d 31e 31f 320 321 322 323 324 325 326 327 328 329 32a 32b 32c 32d 32e 32f 330
  //   331 332 333 334 335 336 337 338 339 33a 33b 33c 33d 33e 33f 340 341 342 343 344 345 346 347 348 349
  //   34a 34b 34c 34d 34e 34f 350 351 352 353 354 355 356 357 358 359 35a 35b 35c 35d 35e 35f 360 361 362
  //   363 364 365 366 367 368 369 36a 36b 36c 36d 36e 36f 370 371 372 373 374 375 376 377 378 379 37a 37b
  //   37c 37d 37e 37f 380 381 382 383 384 385 386 387 388 389 38a 38b 38c 38d 38e 38f 390 391 392 393 394
  //   395 396 397 398 399 39a 39b 39c 39d 39e 39f 3a0 3a1 3a2 3a3 3a4 3a5 3a6 3a7 3a8 3a9 3aa 3ab 3ac 3ad
  //   3ae 3af 3b0 3b1 3b2 3b3 3b4 3b5 3b6 3b7 3b8 3b9 3ba 3bb 3bc 3bd 3be 3bf 3c0 3c1 3c2 3c3 3c4 3c5 3c6
  //   3c7 3c8 3c9 3ca 3cb 3cc 3cd 3ce 3cf 3d0 3d1 3d2 3d3 3d4 3d5 3d6 3d7 3d8 3d9 3da 3db 3dc 3dd 3de 3df
  //   3e0 3e1 3e2 3e3 3e4 3e5 3e6 3e7 3e8 3e9 3ea 3eb 3ec 3ed 3ee 3ef 3f0 3f1 3f2 3f3 3f4 3f5 3f6 3f7 3f8
  //   3f9 3fa 3fb 3fc 3fd 3fe 3ff 400 401 402 403 404 405 406 407 408 409 40a 40b 40c 40d 40e 40f 410 411
  //   412 413 414 415 416 417 418 419 41a 41b 41c 41d 41e 41f 420 421 422 423 424 425 426 427 428 429 42a
  //   42b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
  //   contents of rom_2 (hex, n*v repeats v):
  //   0 1 0 1 0 1 0 9*1 0 1 0 1 0 1 0 9*1 0 1 0 1 0 1 0 9*1 0 1 0 1 0 1 0 9*1 0 1 0 1 0 1 0 9*1 0 1 0 1 0
  //   1 0 9*1 0 1 0 1 0 1 0 9*1 0 1 0 1 0 1 0 9*1 16*0 16*1 16*0 16*1 16*0 16*1 16*0 16*1 0 0 1 1 0 0 1 1
  //   0 0 1 1 0 0 1 1 0 0 1 1 0 0 1 1 0 0 1 1 0 0 34*1 0 0 1 1 0 0 1 1 0 0 1 1 0 0 1 1 0 0 1 1 0 0 1 1 0 0
  //   1 1 0 0 34*1 4*0 4*1 4*0 4*1 4*0 4*1 4*0 4*1 4*0 4*1 4*0 4*1 4*0 4*1 4*0 68*1 0 1 0 1 0 1 0 9*1 0 1
  //   0 1 0 1 0 9*1 0 1 0 1 0 1 0 9*1 0 1 0 1 0 1 0 9*1 0 1 0 1 0 1 0 9*1 0 1 0 1 0 1 0 9*1 0 1 0 1 0 1 0
  //   9*1 0 1 0 1 0 1 0 9*1 16*0 16*1 16*0 16*1 16*0 16*1 16*0 16*1 0 0 1 1 0 0 1 1 0 0 1 1 0 0 1 1 0 0 1
  //   1 0 0 1 1 0 0 1 1 0 0 1 1 0 0 1 1 0 0 1 1 0 0 1 1 0 0 1 1 0 0 1 1 0 0 1 1 0 0 1 1 0 0 1 1 0 0 1 1 0
  //   0 1 1 0 0 1 1 0 0 1 1 0 0 1 1 0 0 1 1 0 0 1 1 0 0 1 1 0 0 1 1 0 0 1 1 0 0 1 1 0 0 1 1 0 0 1 1 0 0 1
  //   1 0 0 1 1 0 0 1 1 4*0 4*1 4*0 4*1 4*0 4*1 4*0 4*1 4*0 4*1 4*0 4*1 4*0 4*1 4*0 68*1 0 1 0 1 0 1 0 9*1
  //   0 1 0 1 0 1 0 9*1 0 1 0 1 0 1 0 9*1 0 1 0 1 0 1 0 9*1 0 1 0 1 0 1 0 9*1 0 1 0 1 0 1 0 9*1 0 1 0 1 0
  //   1 0 9*1 0 1 0 1 0 1 0 9*1 130*0 1 1 0 0 1 1 0 0 1 1 0 0 1 1 0 0 1 1 0 0 1 1 0 0 1 1 0 0 34*1 0 0 1 1
  //   0 0 1 1 0 0 1 1 0 0 1 1 0 0 1 1 0 0 1 1 0 0 1 1 0 0 34*1 4*0 4*1 4*0 4*1 4*0 4*1 4*0 4*1 4*0 4*1 4*0
  //   4*1 4*0 4*1 4*0 68*1 0 1 0 1 0 1 0 9*1 0 1 0 1 0 1 0 9*1 0 1 0 1 0 1 0 9*1 0 1 0 1 0 1 0 9*1 0 1 0 1
  //   0 1 0 9*1 0 1 0 1 0 1 0 9*1 0 1 0 1 0 1 0 9*1 0 1 0 1 0 1 0 9*1 130*0 1 1 0 0 1 1 0 0 1 1 0 0 1 1 0
  //   0 1 1 0 0 1 1 0 0 1 1 0 0 1 1 0 0 1 1 0 0 1 1 0 0 1 1 0 0 1 1 0 0 1 1 0 0 1 1 0 0 1 1 0 0 1 1 0 0 1
  //   1 0 0 1 1 0 0 1 1 0 0 1 1 0 0 1 1 0 0 1 1 0 0 1 1 0 0 1 1 0 0 1 1 0 0 1 1 0 0 1 1 0 0 1 1 0 0 1 1 0
  //   0 1 1 0 0 1 1 0 0 1 1 4*0 4*1 4*0 4*1 4*0 4*1 4*0 4*1 4*0 4*1 4*0 4*1 4*0 4*1 4*0 68*1 0 1 0 1 0 1 0
  //   9*1 0 1 0 1 0 1 0 9*1 0 1 0 1 0 1 0 9*1 0 1 0 1 0 1 0 9*1 0 1 0 1 0 1 0 9*1 0 1 0 1 0 1 0 9*1 0 1 0
  //   1 0 1 0 9*1 0 1 0 1 0 1 0 9*1 16*0 16*1 16*0 16*1 16*0 16*1 16*0 144*1 4*0 4*1 4*0 4*1 4*0 4*1 4*0
  //   4*1 4*0 4*1 4*0 4*1 4*0 4*1 4*0 68*1 0 1 0 1 0 1 0 9*1 0 1 0 1 0 1 0 9*1 0 1 0 1 0 1 0 9*1 0 1 0 1 0
  //   1 0 9*1 0 1 0 1 0 1 0 9*1 0 1 0 1 0 1 0 9*1 0 1 0 1 0 1 0 9*1 0 1 0 1 0 1 0 9*1 16*0 16*1 16*0 16*1
  //   16*0 16*1 16*0 144*1 4*0 4*1 4*0 4*1 4*0 4*1 4*0 4*1 4*0 4*1 4*0 4*1 4*0 4*1 4*0 68*1 0 1 0 1 0 1 0
  //   9*1 0 1 0 1 0 1 0 9*1 0 1 0 1 0 1 0 9*1 0 1 0 1 0 1 0 9*1 0 1 0 1 0 1 0 9*1 0 1 0 1 0 1 0 9*1 0 1 0
  //   1 0 1 0 9*1 0 1 0 1 0 1 0 9*1 130*0 1 1 0 0 1 1 0 0 1 1 0 0 1 1 0 0 1 1 0 0 1 1 0 0 1 1 0 0 34*1 0 0
  //   1 1 0 0 1 1 0 0 1 1 0 0 1 1 0 0 1 1 0 0 1 1 0 0 1 1 0 0 34*1 4*0 4*1 4*0 4*1 4*0 4*1 4*0 4*1 4*0 4*1
  //   4*0 4*1 4*0 4*1 4*0 68*1 0 1 0 1 0 1 0 9*1 0 1 0 1 0 1 0 9*1 0 1 0 1 0 1 0 9*1 0 1 0 1 0 1 0 9*1 0 1
  //   0 1 0 1 0 9*1 0 1 0 1 0 1 0 9*1 0 1 0 1 0 1 0 9*1 0 1 0 1 0 1 0 9*1 130*0 1 1 0 0 1 1 0 0 1 1 0 0 1
  //   1 0 0 1 1 0 0 1 1 0 0 1 1 0 0 1 1 0 0 1 1 0 0 1 1 0 0 1 1 0 0 1 1 0 0 1 1 0 0 1 1 0 0 1 1 0 0 1 1 0
  //   0 1 1 0 0 1 1 0 0 1 1 0 0 1 1 0 0 1 1 0 0 1 1 0 0 1 1 0 0 1 1 0 0 1 1 0 0 1 1 0 0 1 1 0 0 1 1 0 0 1
  //   1 0 0 1 1 0 0 1 1 0 0 1 1 4*0 4*1 4*0 4*1 4*0 4*1 4*0 4*1 4*0 4*1 4*0 4*1 4*0 4*1 4*0 68*1 0 1 0 1 0
  //   1 0 9*1 0 1 0 1 0 1 0 9*1 0 1 0 1 0 1 0 9*1 0 1 0 1 0 1 0 9*1 0 1 0 1 0 1 0 9*1 0 1 0 1 0 1 0 9*1 0
  //   1 0 1 0 1 0 9*1 0 1 0 1 0 1 0 137*1 0 0 1 1 0 0 1 1 0 0 1 1 0 0 1 1 0 0 1 1 0 0 1 1 0 0 1 1 0 0 34*1
  //   0 0 1 1 0 0 1 1 0 0 1 1 0 0 1 1 0 0 1 1 0 0 1 1 0 0 1 1 0 0 34*1 4*0 4*1 4*0 4*1 4*0 4*1 4*0 4*1 4*0
  //   4*1 4*0 4*1 4*0 4*1 4*0 68*1 0 1 0 1 0 1 0 9*1 0 1 0 1 0 1 0 9*1 0 1 0 1 0 1 0 9*1 0 1 0 1 0 1 0 9*1
  //   0 1 0 1 0 1 0 9*1 0 1 0 1 0 1 0 9*1 0 1 0 1 0 1 0 9*1 0 1 0 1 0 1 0 137*1 0 0 1 1 0 0 1 1 0 0 1 1 0
  //   0 1 1 0 0 1 1 0 0 1 1 0 0 1 1 0 0 1 1 0 0 1 1 0 0 1 1 0 0 1 1 0 0 1 1 0 0 1 1 0 0 1 1 0 0 1 1 0 0 1
  //   1 0 0 1 1 0 0 1 1 0 0 1 1 0 0 1 1 0 0 1 1 0 0 1 1 0 0 1 1 0 0 1 1 0 0 1 1 0 0 1 1 0 0 1 1 0 0 1 1 0
  //   0 1 1 0 0 1 1 0 0 1 1 0 0 1 1 4*0 4*1 4*0 4*1 4*0 4*1 4*0 4*1 4*0 4*1 4*0 4*1 4*0 4*1 4*0 68*1 0 1 0
  //   1 0 1 0 9*1 0 1 0 1 0 1 0 9*1 0 1 0 1 0 1 0 9*1 0 1 0 1 0 1 0 9*1 0 1 0 1 0 1 0 9*1 0 1 0 1 0 1 0
  //   9*1 0 1 0 1 0 1 0 9*1 0 1 0 1 0 1 0 137*1 0 0 1 1 0 0 1 1 0 0 1 1 0 0 1 1 0 0 1 1 0 0 1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
  //   错误记录X&Y
  //   存储器保存未通过的测试用例
  //   ctrl+K驱动时钟自动测试
endmodule

module \电梯上下停开状态计算  (
  input  S0,
  input  S1,
  input  OP,
  input  OP_M,
  input  CL_M,
  input  UP,
  input  DOWN,
  input  TIMEUP,
  output N0,
  output N1
);

  wire and_1_out, and_2_out, and_3_out, and_4_out, and_5_out, and_6_out, and_7_out, and_8_out, and_9_out,
       and_10_out, and_11_out, and_12_out, and_13_out, and_14_out, not_1_out, not_2_out, not_3_out,
       not_4_out, not_5_out, not_6_out, not_7_out, not_8_out, not_9_out, not_10_out, not_11_out, not_12_out,
       not_13_out, not_14_out, not_15_out, not_16_out, not_17_out, not_18_out, not_19_out, not_20_out,
       not_21_out, not_22_out, not_23_out, not_24_out, not_25_out, not_26_out, not_27_out, not_28_out,
       not_29_out, not_30_out, not_31_out, not_32_out, not_33_out, not_34_out, not_35_out, not_36_out,
       not_37_out, not_38_out, not_39_out, not_40_out, not_41_out, not_42_out, not_43_out, not_44_out,
       not_45_out, not_46_out, not_47_out;

  not not_1 (not_1_out, S1);
  not not_2 (not_2_out, S0);
  not not_3 (not_3_out, OP);
  not not_4 (not_4_out, OP_M);
  not not_5 (not_5_out, S0);
  not not_6 (not_6_out, S1);
  not not_7 (not_7_out, S1);
  not not_8 (not_8_out, OP);
  not not_9 (not_9_out, S1);
  not not_10 (not_10_out, S1);
  not not_11 (not_11_out, S1);
  not not_12 (not_12_out, S0);
  not not_13 (not_13_out, S0);
  not not_14 (not_14_out, S1);
  not not_15 (not_15_out, S0);
  not not_16 (not_16_out, S0);
  not not_17 (not_17_out, S1);
  not not_18 (not_18_out, S1);
  not not_19 (not_19_out, S0);
  not not_20 (not_20_out, S0);
  not not_21 (not_21_out, S1);
  not not_22 (not_22_out, CL_M);
  not not_23 (not_23_out, TIMEUP);
  not not_24 (not_24_out, S1);
  not not_25 (not_25_out, S0);
  not not_26 (not_26_out, OP);
  not not_27 (not_27_out, OP_M);
  not not_28 (not_28_out, UP);
  not not_29 (not_29_out, S0);
  not not_30 (not_30_out, S1);
  not not_31 (not_31_out, S1);
  not not_32 (not_32_out, S1);
  not not_33 (not_33_out, S0);
  not not_34 (not_34_out, S0);
  not not_35 (not_35_out, S0);
  not not_36 (not_36_out, OP);
  not not_37 (not_37_out, S0);
  not not_38 (not_38_out, S1);
  not not_39 (not_39_out, S0);
  not not_40 (not_40_out, S0);
  not not_41 (not_41_out, S1);
  not not_42 (not_42_out, S1);
  not not_43 (not_43_out, S0);
  not not_44 (not_44_out, S0);
  not not_45 (not_45_out, S1);
  not not_46 (not_46_out, CL_M);
  not not_47 (not_47_out, TIMEUP);
  and and_1 (and_1_out, not_1_out, not_2_out, not_3_out, not_4_out, UP, not_5_out, not_6_out);
  and and_2 (and_2_out, not_7_out, S0, not_8_out, UP, S0, not_9_out);
  and and_3 (and_3_out, not_10_out, S0, OP, S0, not_11_out);
  and and_4 (and_4_out, S1, not_12_out, OP, not_13_out, S1);
  and and_5 (and_5_out, not_14_out, not_15_out, OP, not_16_out, not_17_out);
  and and_6 (and_6_out, not_18_out, not_19_out, OP_M, not_20_out, not_21_out);
  and and_7 (and_7_out, S1, S0, not_22_out, not_23_out, S0, S1);
  and and_8 (and_8_out, not_24_out, not_25_out, not_26_out, not_27_out, not_28_out, DOWN, not_29_out, not_30_out);
  and and_9 (and_9_out, not_31_out, S0, OP, S0, not_32_out);
  and and_10 (and_10_out, S1, not_33_out, OP, not_34_out, S1);
  and and_11 (and_11_out, S1, not_35_out, not_36_out, DOWN, not_37_out, S1);
  and and_12 (and_12_out, not_38_out, not_39_out, OP, not_40_out, not_41_out);
  and and_13 (and_13_out, not_42_out, not_43_out, OP_M, not_44_out, not_45_out);
  and and_14 (and_14_out, S1, S0, not_46_out, not_47_out, S0, S1);
  or or_1 (N0, and_1_out, and_2_out, and_3_out, and_4_out, and_5_out, and_6_out, and_7_out);
  or or_2 (N1, and_8_out, and_9_out, and_10_out, and_11_out, and_12_out, and_13_out, and_14_out);
endmodule

module \电梯上下停开状态计算测试  (
  output [15:0] Cnt,
  output [1:0] S1S0,
  output OP,
  output OP_M,
  output CL_M,
  output UP,
  output DOWN,
  output TIMEUP,
  output [1:0] N1N0,
  output _passed,
  output halt
);

  wire and_1_out, CLK, d_ff_1_q, d_ff_1_qn, NEQ, nHalt;
  wire [1:0] output_t;
  wire [9:0] counter_2_q;
  wire [15:0] multiplexer_1_out, multiplexer_1_out_2;
  wire [31:0] XY;

  Clock #(.highDuration(1), .lowDuration(1)) clock_1 (.out(CLK));
  Counter #(.width(16), .max('hffff), .ongoal("wrap"), .trigger("rising"), .behavior("old")) counter_1 (
    .count(nHalt), .Q(Cnt), .clk(CLK));  // open: load, D, carry, clr, preset
  // Probe on Cnt
  // Probe on Cnt
  // Probe on 16'hff
  Comparator #(.width(16), .mode("twosComplement")) comparator_1 (.a(Cnt), .b(16'hff), .eq(halt));  // open: gt, lt
  ROM #(.addrWidth(16), .dataWidth(8), .Select("high")) rom_1 (
    .addr(Cnt), .data({TIMEUP, DOWN, UP, CL_M, OP_M, OP, S1S0}));
  ROM #(.addrWidth(16), .dataWidth(2), .Select("high")) rom_2 (.addr(Cnt), .data(output_t));
  not not_1 (nHalt, halt);
  RAM #(.addrWidth(16), .dataWidth(2), .bus("separate"), .Select("low")) ram_1 (
    .addr(Cnt), .din(N1N0), .str(nHalt), .clk(CLK));  // open: data, sel, ld, clr
  not not_2 (NEQ, _passed);
  LED #(.active("true")) \u_测试完成  (.in(halt));
  Counter #(.width(10), .max('h3ff), .ongoal("wrap"), .trigger("rising"), .behavior("old")) counter_2 (
    .count(NEQ), .Q(counter_2_q), .clk(CLK), .clr(halt));  // open: load, D, carry, preset
  and and_1 (and_1_out, ~halt, NEQ);  // AND_Gate
  Pull_Resistor #(.pull(0)) pull_resistor_1 (.node(_passed));
  Comparator #(.width(2), .mode("twosComplement")) comparator_2 (.a(output_t), .b(N1N0), .eq(_passed));  // open: gt, lt
  // 电梯上下停开状态计算 电梯上下停开状态计算_1: pin names not known; wires that end beside it: S1S0[0], S1S0[1], OP, OP_M, CL_M, UP, DOWN
  RAM #(.addrWidth(10), .dataWidth(32), .bus("separate"), .Select("high")) ram_2 (
    .addr(counter_2_q), .din(XY), .str(and_1_out), .clk(CLK));  // open: data, sel, ld, clr
  _7_Segment_Display #(.active("true")) u_7_segment_display_1 (
    .g(multiplexer_1_out[11]), .f(multiplexer_1_out[10]), .a(multiplexer_1_out[9]), .b(multiplexer_1_out[8]),
    .e(multiplexer_1_out_2[11]), .d(multiplexer_1_out_2[10]), .c(multiplexer_1_out_2[9]),
    .dp(multiplexer_1_out_2[8]));
  _7_Segment_Display #(.active("true")) u_7_segment_display_2 (
    .g(multiplexer_1_out[15]), .f(multiplexer_1_out[14]), .a(multiplexer_1_out[13]),
    .b(multiplexer_1_out[12]), .e(multiplexer_1_out_2[15]), .d(multiplexer_1_out_2[14]),
    .c(multiplexer_1_out_2[13]), .dp(multiplexer_1_out_2[12]));
  D_Flip_Flop #(.trigger("rising"), .Pre_Clr_Positions("LEGACY"), .NegatePresetClear("false"), .enable("true"), .NewFFLayout("false")) d_ff_1 (
    .clk(CLK), .D(NEQ), .Q(d_ff_1_q), .Qn(d_ff_1_qn), .en(d_ff_1_qn));  // open: preset, reset
  _7_Segment_Display #(.active("true")) u_7_segment_display_3 (
    .g(multiplexer_1_out[7]), .f(multiplexer_1_out[6]), .a(multiplexer_1_out[5]), .b(multiplexer_1_out[4]),
    .e(multiplexer_1_out_2[7]), .d(multiplexer_1_out_2[6]), .c(multiplexer_1_out_2[5]),
    .dp(multiplexer_1_out_2[4]));
  _7_Segment_Display #(.active("true")) u_7_segment_display_4 (
    .g(multiplexer_1_out[3]), .f(multiplexer_1_out[2]), .a(multiplexer_1_out[1]), .b(multiplexer_1_out[0]),
    .e(multiplexer_1_out_2[3]), .d(multiplexer_1_out_2[2]), .c(multiplexer_1_out_2[1]),
    .dp(multiplexer_1_out_2[0]));
  Multiplexer #(.select(1), .width(32), .disabled(0), .enable("true")) multiplexer_1 (
    .in0(32'h8a66ffee), .in1(32'h8a8cef44), .out({multiplexer_1_out_2, multiplexer_1_out}), .sel(d_ff_1_q),
    .en(halt));

  // Other names for the same wires on the sheet: Equal = _passed;
  //   input[7:0] = {TIMEUP, DOWN, UP, CL_M, OP_M, OP, S1S0}; Output[1:0] = N1N0; tunnel[15:0] = Cnt

  // Notes on the sheet:
  //   测试节拍数
  //   contents of rom_1 (hex, n*v repeats v):
  //   0 1 2 3 4 5 6 7 8 9 a b c d e f 10 11 12 13 14 15 16 17 18 19 1a 1b 1c 1d 1e 1f 20 21 22 23 24 25 26
  //   27 28 29 2a 2b 2c 2d 2e 2f 30 31 32 33 34 35 36 37 38 39 3a 3b 3c 3d 3e 3f 40 41 42 43 44 45 46 47
  //   48 49 4a 4b 4c 4d 4e 4f 50 51 52 53 54 55 56 57 58 59 5a 5b 5c 5d 5e 5f 60 61 62 63 64 65 66 67 68
  //   69 6a 6b 6c 6d 6e 6f 70 71 72 73 74 75 76 77 78 79 7a 7b 7c 7d 7e 7f 80 81 82 83 84 85 86 87 88 89
  //   8a 8b 8c 8d 8e 8f 90 91 92 93 94 95 96 97 98 99 9a 9b 9c 9d 9e 9f a0 a1 a2 a3 a4 a5 a6 a7 a8 a9 aa
  //   ab ac ad ae af b0 b1 b2 b3 b4 b5 b6 b7 b8 b9 ba bb bc bd be bf c0 c1 c2 c3 c4 c5 c6 c7 c8 c9 ca cb
  //   cc cd ce cf d0 d1 d2 d3 d4 d5 d6 d7 d8 d9 da db dc dd de df e0 e1 e2 e3 e4 e5 e6 e7 e8 e9 ea eb ec
  //   ed ee ef f0 f1 f2 f3 f4 f5 f6 f7 f8 f9 fa fb fc fd fe ff
  //   contents of rom_2 (hex, n*v repeats v):
  //   0 0 0 6*3 0 0 5*3 4*0 3 3 3 0 3 0 0 0 3 3 3 0 1 1 0 6*3 1 0 5*3 1 1 0 0 3 3 3 0 3 1 0 0 3 3 3 0 2 0
  //   2 6*3 0 2 5*3 2 0 2 0 3 3 3 0 3 0 2 0 3 3 3 4*0 6*3 0 0 5*3 4*0 3 3 3 0 3 0 0 0 3 3 3 5*0 3 3 3 0 3
  //   0 0 0 3 3 3 5*0 3 3 3 0 3 0 0 0 3 3 3 0 1 1 0 0 3 3 3 0 3 1 0 0 3 3 3 0 1 1 0 0 3 3 3 0 3 1 0 0 3 3
  //   3 0 2 0 2 0 3 3 3 0 3 0 2 0 3 3 3 0 2 0 2 0 3 3 3 0 3 0 2 0 3 3 3 5*0 3 3 3 0 3 0 0 0 3 3 3 5*0 3 3
  //   3 0 3 0 0 0 3 3 3
  //   错误记录X&Y
  //   存储器保存未通过的测试用例
  //   ctrl+K驱动时钟自动测试
endmodule

module \电梯上下停开状态转移  (
  input  \手动关门 ,
  input  \上升 ,
  input  \手动开门 ,
  input  \下降 ,
  input  \其他输入引起的开门请求 ,
  input  \开门时间到 ,
  output \开门 ,
  output out_8,
  output out_9
);

  wire CLK, \电梯上下停开状态计算_1_n0 , \电梯上下停开状态计算_1_n1 ;

  Clock #(.highDuration(1), .lowDuration(1)) clock_1 (.out(CLK));
  \电梯上下停开状态计算  \u_电梯上下停开状态计算_1  (
    .S0(out_8), .S1(out_9), .OP(\其他输入引起的开门请求 ), .OP_M(\手动开门 ), .CL_M(\手动关门 ), .UP(\上升 ), .DOWN(\下降 ),
    .TIMEUP(\开门时间到 ), .N0(\电梯上下停开状态计算_1_n0 ), .N1(\电梯上下停开状态计算_1_n1 ));
  D_Flip_Flop #(.trigger("rising"), .Pre_Clr_Positions("ABOVE_BELOW"), .NegatePresetClear("false"), .enable("false"), .NewFFLayout("true")) d_ff_1 (
    .clk(CLK), .D(\电梯上下停开状态计算_1_n0 ), .Q(out_8));  // open: Qn, preset, reset
  D_Flip_Flop #(.trigger("rising"), .Pre_Clr_Positions("ABOVE_BELOW"), .NegatePresetClear("false"), .enable("false"), .NewFFLayout("true")) d_ff_2 (
    .clk(CLK), .D(\电梯上下停开状态计算_1_n1 ), .Q(out_9));  // open: Qn, preset, reset
  and and_1 (\开门 , out_9, out_8);

  // Other names for the same wires on the sheet: QA = out_8; QB = out_9; 开_关门 = \开门 ; 开门请求 = \其他输入引起的开门请求 

  // Notes on the sheet:
  //   输入
  //   输出
endmodule

module \电梯上下停开状态转移测试  (
  output [15:0] Cnt,
  output CL_M,
  output OP_M,
  output UP,
  output DOWN,
  output OP,
  output TIMEUP,
  output [1:0] QBQA,
  output \开_关门 ,
  output _passed,
  output halt
);

  wire and_1_out, CLK, d_ff_1_q, d_ff_1_qn, NEQ, nHalt;
  wire [2:0] output_t;
  wire [9:0] counter_2_q;
  wire [15:0] multiplexer_1_out, multiplexer_1_out_2;
  wire [31:0] XY;

  Clock #(.highDuration(1), .lowDuration(1)) clock_1 (.out(CLK));
  Counter #(.width(16), .max('hffff), .ongoal("wrap"), .trigger("rising"), .behavior("old")) counter_1 (
    .count(nHalt), .Q(Cnt), .clk(CLK));  // open: load, D, carry, clr, preset
  // Probe on Cnt
  // Probe on Cnt
  // Probe on 16'h4a
  Comparator #(.width(16), .mode("twosComplement")) comparator_1 (.a(Cnt), .b(16'h4a), .eq(halt));  // open: gt, lt
  ROM #(.addrWidth(16), .dataWidth(6), .Select("high")) rom_1 (.addr(Cnt), .data({TIMEUP, OP, DOWN, UP, OP_M, CL_M}));
  ROM #(.addrWidth(16), .dataWidth(3), .Select("high")) rom_2 (.addr(Cnt), .data(output_t));
  not not_1 (nHalt, halt);
  RAM #(.addrWidth(16), .dataWidth(3), .bus("separate"), .Select("low")) ram_1 (
    .addr(Cnt), .din({\开_关门 , QBQA}), .str(nHalt), .clk(CLK));  // open: data, sel, ld, clr
  not not_2 (NEQ, _passed);
  LED #(.active("true")) \u_测试完成  (.in(halt));
  Counter #(.width(10), .max('h3ff), .ongoal("wrap"), .trigger("rising"), .behavior("old")) counter_2 (
    .count(NEQ), .Q(counter_2_q), .clk(CLK), .clr(halt));  // open: load, D, carry, preset
  and and_1 (and_1_out, ~halt, NEQ);  // AND_Gate
  Pull_Resistor #(.pull(0)) pull_resistor_1 (.node(_passed));
  Comparator #(.width(3), .mode("twosComplement")) comparator_2 (
    .a(output_t), .b({\开_关门 , QBQA}), .eq(_passed));  // open: gt, lt
  \电梯上下停开状态转移  \u_电梯上下停开状态转移_1  (
    .\手动关门 (CL_M), .\上升 (UP), .\手动开门 (OP_M), .\下降 (DOWN), .\其他输入引起的开门请求 (OP), .\开门时间到 (TIMEUP),
    .\开门 (\开_关门 ), .out_8(QBQA[0]), .out_9(QBQA[1]));
  RAM #(.addrWidth(10), .dataWidth(32), .bus("separate"), .Select("high")) ram_2 (
    .addr(counter_2_q), .din(XY), .str(and_1_out), .clk(CLK));  // open: data, sel, ld, clr
  _7_Segment_Display #(.active("true")) u_7_segment_display_1 (
    .g(multiplexer_1_out[15]), .f(multiplexer_1_out[14]), .a(multiplexer_1_out[13]),
    .b(multiplexer_1_out[12]), .e(multiplexer_1_out_2[15]), .d(multiplexer_1_out_2[14]),
    .c(multiplexer_1_out_2[13]), .dp(multiplexer_1_out_2[12]));
  _7_Segment_Display #(.active("true")) u_7_segment_display_2 (
    .g(multiplexer_1_out[11]), .f(multiplexer_1_out[10]), .a(multiplexer_1_out[9]), .b(multiplexer_1_out[8]),
    .e(multiplexer_1_out_2[11]), .d(multiplexer_1_out_2[10]), .c(multiplexer_1_out_2[9]),
    .dp(multiplexer_1_out_2[8]));
  D_Flip_Flop #(.trigger("rising"), .Pre_Clr_Positions("LEGACY"), .NegatePresetClear("false"), .enable("true"), .NewFFLayout("false")) d_ff_1 (
    .clk(CLK), .D(NEQ), .Q(d_ff_1_q), .Qn(d_ff_1_qn), .en(d_ff_1_qn));  // open: preset, reset
  _7_Segment_Display #(.active("true")) u_7_segment_display_3 (
    .g(multiplexer_1_out[3]), .f(multiplexer_1_out[2]), .a(multiplexer_1_out[1]), .b(multiplexer_1_out[0]),
    .e(multiplexer_1_out_2[3]), .d(multiplexer_1_out_2[2]), .c(multiplexer_1_out_2[1]),
    .dp(multiplexer_1_out_2[0]));
  _7_Segment_Display #(.active("true")) u_7_segment_display_4 (
    .g(multiplexer_1_out[7]), .f(multiplexer_1_out[6]), .a(multiplexer_1_out[5]), .b(multiplexer_1_out[4]),
    .e(multiplexer_1_out_2[7]), .d(multiplexer_1_out_2[6]), .c(multiplexer_1_out_2[5]),
    .dp(multiplexer_1_out_2[4]));
  Multiplexer #(.select(1), .width(32), .disabled(0), .enable("true")) multiplexer_1 (
    .in0(32'h8a66ffee), .in1(32'h8a8cef44), .out({multiplexer_1_out_2, multiplexer_1_out}), .sel(d_ff_1_q),
    .en(halt));

  // Other names for the same wires on the sheet: Equal = _passed; input[5:0] = {TIMEUP, OP, DOWN, UP, OP_M, CL_M};
  //   手动关门 = CL_M; 手动开门 = OP_M; 上升 = UP; 下降 = DOWN; 开门请求 = OP; 开门时间到 = TIMEUP; Output[2:0] = {\开_关门 , QBQA};
  //   开门 = \开_关门 ; QA = QBQA[0]; QB = QBQA[1]; tunnel[15:0] = Cnt

  // Notes on the sheet:
  //   测试节拍数
  //   contents of rom_1 (hex, n*v repeats v):
  //   0 0 0 4*10 0 0 20 20 0 0 2 2 0 1 1 1 0 5*4 6 4 5 4 14 14 14 4 24 24 4 4 4 14 14 14 4 4 0 0 0 20 20
  //   4*8 6*18 8 28 6*8 18 4*10 0 0 20 20
  //   contents of rom_2 (hex, n*v repeats v):
  //   4*0 6*7 4*0 7 7 7 4*0 9*1 4*7 0 4*1 8*7 0 0 4*2 7*7 0 6*2 7*7
  //   错误记录X&Y
  //   存储器保存未通过的测试用例
  //   ctrl+K驱动时钟自动测试
endmodule

module \模五计数器  (
  input  in_1,
  input  in_2,
  input  in_3,
  output \零 ,
  output out_5,
  output out_6,
  output out_7
);

  wire and_1_out, and_2_out, and_3_out, and_4_out, and_5_out, and_6_out, and_7_out, CLK, d_ff_2_qn,
       d_ff_3_qn, not_1_out, not_2_out, not_3_out, not_4_out, not_5_out, or_1_out, or_2_out, or_3_out, \重置 ;

  Clock #(.highDuration(1), .lowDuration(1)) clock_1 (.out(CLK));
  not not_1 (not_1_out, in_1);
  not not_2 (not_2_out, in_1);
  and and_1 (and_1_out, in_1, out_7, out_6);
  and and_2 (and_2_out, out_6, d_ff_3_qn);
  and and_3 (and_3_out, not_1_out, out_6);
  and and_4 (and_4_out, in_1, out_7, d_ff_2_qn);
  and and_5 (and_5_out, out_7, not_2_out);
  and and_6 (and_6_out, in_1, d_ff_3_qn);
  not not_3 (not_3_out, out_6);
  or or_1 (or_1_out, out_5, and_1_out);
  or or_2 (or_2_out, and_2_out, and_3_out, and_4_out);
  or or_3 (or_3_out, and_5_out, and_6_out);
  and and_7 (and_7_out, out_5, not_3_out, out_7);
  or or_4 (\重置 , and_7_out, in_3);
  D_Flip_Flop #(.trigger("rising"), .Pre_Clr_Positions("ABOVE_BELOW"), .NegatePresetClear("false"), .enable("true"), .NewFFLayout("true")) d_ff_1 (
    .clk(CLK), .D(or_1_out), .Q(out_5), .en(in_2), .reset(\重置 ));  // open: Qn, preset
  D_Flip_Flop #(.trigger("rising"), .Pre_Clr_Positions("ABOVE_BELOW"), .NegatePresetClear("false"), .enable("true"), .NewFFLayout("true")) d_ff_2 (
    .clk(CLK), .D(or_2_out), .Q(out_6), .Qn(d_ff_2_qn), .en(in_2), .reset(\重置 ));  // open: preset
  D_Flip_Flop #(.trigger("rising"), .Pre_Clr_Positions("ABOVE_BELOW"), .NegatePresetClear("false"), .enable("true"), .NewFFLayout("true")) d_ff_3 (
    .clk(CLK), .D(or_3_out), .Q(out_7), .Qn(d_ff_3_qn), .en(in_2), .reset(\重置 ));  // open: preset
  // Probe on {out_5, out_6, out_7}
  not not_4 (not_4_out, out_6);
  not not_5 (not_5_out, out_7);
  and and_8 (\零 , out_5, not_4_out, not_5_out);

  // Other names for the same wires on the sheet: QA = out_7; QB = out_6; QC = out_5; EN = in_2; 加 = in_1; 手动重置 = in_3
endmodule

module \模五计数器测试  (
  output [15:0] Cnt,
  output en,
  output add,
  output reset,
  output [2:0] count,
  output zero,
  output _passed,
  output halt
);

  wire and_1_out, CLK, d_ff_1_q, d_ff_1_qn, NEQ, nHalt;
  wire [3:0] output_t;
  wire [9:0] counter_2_q;
  wire [15:0] multiplexer_1_out, multiplexer_1_out_2;
  wire [31:0] XY;

  Clock #(.highDuration(1), .lowDuration(1)) clock_1 (.out(CLK));
  Counter #(.width(16), .max('hffff), .ongoal("wrap"), .trigger("rising"), .behavior("old")) counter_1 (
    .count(nHalt), .Q(Cnt), .clk(CLK));  // open: load, D, carry, clr, preset
  // Probe on Cnt
  // Probe on Cnt
  // Probe on 16'h30
  Comparator #(.width(16), .mode("twosComplement")) comparator_1 (.a(Cnt), .b(16'h30), .eq(halt));  // open: gt, lt
  ROM #(.addrWidth(16), .dataWidth(3), .Select("high")) rom_1 (.addr(Cnt), .data({reset, add, en}));
  ROM #(.addrWidth(16), .dataWidth(4), .Select("high")) rom_2 (.addr(Cnt), .data(output_t));
  not not_1 (nHalt, halt);
  RAM #(.addrWidth(16), .dataWidth(4), .bus("separate"), .Select("low")) ram_1 (
    .addr(Cnt), .din({zero, count}), .str(nHalt), .clk(CLK));  // open: data, sel, ld, clr
  not not_2 (NEQ, _passed);
  LED #(.active("true")) \u_测试完成  (.in(halt));
  Counter #(.width(10), .max('h3ff), .ongoal("wrap"), .trigger("rising"), .behavior("old")) counter_2 (
    .count(NEQ), .Q(counter_2_q), .clk(CLK), .clr(halt));  // open: load, D, carry, preset
  Pull_Resistor #(.pull(0)) pull_resistor_1 (.node(_passed));
  Comparator #(.width(4), .mode("twosComplement")) comparator_2 (
    .a(output_t), .b({zero, count}), .eq(_passed));  // open: gt, lt
  \模五计数器  \u_模五计数器_1  (
    .in_1(add), .in_2(en), .\零 (zero), .out_5(count[2]), .out_6(count[1]), .out_7(count[0]), .in_3(reset));
  and and_1 (and_1_out, ~halt, NEQ);  // AND_Gate
  RAM #(.addrWidth(10), .dataWidth(32), .bus("separate"), .Select("high")) ram_2 (
    .addr(counter_2_q), .din(XY), .str(and_1_out), .clk(CLK));  // open: data, sel, ld, clr
  _7_Segment_Display #(.active("true")) u_7_segment_display_1 (
    .g(multiplexer_1_out[15]), .f(multiplexer_1_out[14]), .a(multiplexer_1_out[13]),
    .b(multiplexer_1_out[12]), .e(multiplexer_1_out_2[15]), .d(multiplexer_1_out_2[14]),
    .c(multiplexer_1_out_2[13]), .dp(multiplexer_1_out_2[12]));
  D_Flip_Flop #(.trigger("rising"), .Pre_Clr_Positions("LEGACY"), .NegatePresetClear("false"), .enable("true"), .NewFFLayout("false")) d_ff_1 (
    .clk(CLK), .D(NEQ), .Q(d_ff_1_q), .Qn(d_ff_1_qn), .en(d_ff_1_qn));  // open: preset, reset
  _7_Segment_Display #(.active("true")) u_7_segment_display_2 (
    .g(multiplexer_1_out[11]), .f(multiplexer_1_out[10]), .a(multiplexer_1_out[9]), .b(multiplexer_1_out[8]),
    .e(multiplexer_1_out_2[11]), .d(multiplexer_1_out_2[10]), .c(multiplexer_1_out_2[9]),
    .dp(multiplexer_1_out_2[8]));
  _7_Segment_Display #(.active("true")) u_7_segment_display_3 (
    .g(multiplexer_1_out[7]), .f(multiplexer_1_out[6]), .a(multiplexer_1_out[5]), .b(multiplexer_1_out[4]),
    .e(multiplexer_1_out_2[7]), .d(multiplexer_1_out_2[6]), .c(multiplexer_1_out_2[5]),
    .dp(multiplexer_1_out_2[4]));
  _7_Segment_Display #(.active("true")) u_7_segment_display_4 (
    .g(multiplexer_1_out[3]), .f(multiplexer_1_out[2]), .a(multiplexer_1_out[1]), .b(multiplexer_1_out[0]),
    .e(multiplexer_1_out_2[3]), .d(multiplexer_1_out_2[2]), .c(multiplexer_1_out_2[1]),
    .dp(multiplexer_1_out_2[0]));
  Multiplexer #(.select(1), .width(32), .disabled(0), .enable("true")) multiplexer_1 (
    .in0(32'h8a66ffee), .in1(32'h8a8cef44), .out({multiplexer_1_out_2, multiplexer_1_out}), .sel(d_ff_1_q),
    .en(halt));

  // Other names for the same wires on the sheet: Output[3:0] = {zero, count}; QA = count[0]; QB = count[1];
  //   QC = count[2]; Equal = _passed; input[2:0] = {reset, add, en}; tunnel[15:0] = Cnt

  // Notes on the sheet:
  //   测试节拍数
  //   contents of rom_1 (hex, n*v repeats v):
  //   0 0 2 2 2 0 4 0 0 1 19*3 1 1 5 5 5 1 1 1 4*3 2 2 2 6 6 2 2 2
  //   contents of rom_2 (hex, n*v repeats v):
  //   11*0 1 2 3 c 0 1 2 3 c 0 1 2 3 c 0 1 2 3 c c 7*0 1 2 3 c c c
  //   错误记录X&Y
  //   存储器保存未通过的测试用例
  //   ctrl+K驱动时钟自动测试
endmodule

module \楼层计算器  (
  input  in_1,
  input  in_2,
  input  in_3,
  input  in_4,
  output out_5,
  output out_6
);

  wire and_1_out, and_2_out, and_3_out, and_4_out, and_5_out, and_6_out, and_7_out, d_ff_2_qn, not_1_out,
       not_2_out, not_3_out, or_1_out, or_2_out;

  not not_1 (not_1_out, in_4);
  not not_2 (not_2_out, in_4);
  not not_3 (not_3_out, in_3);
  and and_1 (and_1_out, out_5, not_1_out);
  and and_2 (and_2_out, in_3, out_6);
  and and_3 (and_3_out, out_5, out_6);
  and and_4 (and_4_out, out_5, in_3);
  and and_5 (and_5_out, in_3, d_ff_2_qn);
  and and_6 (and_6_out, out_5, in_4, d_ff_2_qn);
  and and_7 (and_7_out, out_6, not_2_out, not_3_out);
  or or_1 (or_1_out, and_1_out, and_2_out, and_3_out);
  or or_2 (or_2_out, and_4_out, and_5_out, and_6_out, and_7_out);
  D_Flip_Flop #(.trigger("rising"), .Pre_Clr_Positions("ABOVE_BELOW"), .NegatePresetClear("false"), .enable("true"), .NewFFLayout("true")) d_ff_1 (
    .clk(in_1), .D(or_1_out), .Q(out_5), .en(in_2));  // open: Qn, preset, reset
  D_Flip_Flop #(.trigger("rising"), .Pre_Clr_Positions("ABOVE_BELOW"), .NegatePresetClear("false"), .enable("true"), .NewFFLayout("true")) d_ff_2 (
    .clk(in_1), .D(or_2_out), .Q(out_6), .Qn(d_ff_2_qn), .en(in_2));  // open: preset, reset
  // Probe on {out_5, out_6}

  // Other names for the same wires on the sheet: QA = out_6; QB = out_5; CLK = in_1; EN = in_2; 减 = in_4; 加 = in_3

  // Notes on the sheet:
  //   高位：
  //   低位：
endmodule

module \楼层计算器测试  (
  output [15:0] Cnt,
  output \平层 ,
  output \开_关门 ,
  output [1:0] QBQA,
  output [1:0] \当前楼层 ,
  output _passed,
  output halt
);

  wire and_1_out, CLK, d_ff_1_q, d_ff_1_qn, NEQ, nHalt, not_3_out;
  wire [1:0] output_t;
  wire [9:0] counter_2_q;
  wire [15:0] multiplexer_1_out, multiplexer_1_out_2;
  wire [31:0] XY;

  Clock #(.highDuration(1), .lowDuration(1)) clock_1 (.out(CLK));
  Counter #(.width(16), .max('hffff), .ongoal("wrap"), .trigger("rising"), .behavior("old")) counter_1 (
    .count(nHalt), .Q(Cnt), .clk(CLK));  // open: load, D, carry, clr, preset
  // Probe on Cnt
  // Probe on Cnt
  // Probe on 16'h2b
  Comparator #(.width(16), .mode("twosComplement")) comparator_1 (.a(Cnt), .b(16'h2b), .eq(halt));  // open: gt, lt
  ROM #(.addrWidth(16), .dataWidth(4), .Select("high")) rom_1 (.addr(Cnt), .data({\开_关门 , QBQA, \平层 }));
  ROM #(.addrWidth(16), .dataWidth(2), .Select("high")) rom_2 (.addr(Cnt), .data(output_t));
  not not_1 (nHalt, halt);
  RAM #(.addrWidth(16), .dataWidth(2), .bus("separate"), .Select("low")) ram_1 (
    .addr(Cnt), .din(\当前楼层 ), .str(nHalt), .clk(CLK));  // open: data, sel, ld, clr
  not not_2 (NEQ, _passed);
  LED #(.active("true")) \u_测试完成  (.in(halt));
  Counter #(.width(10), .max('h3ff), .ongoal("wrap"), .trigger("rising"), .behavior("old")) counter_2 (
    .count(NEQ), .Q(counter_2_q), .clk(CLK), .clr(halt));  // open: load, D, carry, preset
  and and_1 (and_1_out, ~halt, NEQ);  // AND_Gate
  Pull_Resistor #(.pull(0)) pull_resistor_1 (.node(_passed));
  Comparator #(.width(2), .mode("twosComplement")) comparator_2 (
    .a(output_t), .b(\当前楼层 ), .eq(_passed));  // open: gt, lt
  not not_3 (not_3_out, \开_关门 );
  RAM #(.addrWidth(10), .dataWidth(32), .bus("separate"), .Select("high")) ram_2 (
    .addr(counter_2_q), .din(XY), .str(and_1_out), .clk(CLK));  // open: data, sel, ld, clr
  \楼层计算器  \u_楼层计算器_1  (
    .in_1(\平层 ), .in_2(not_3_out), .in_3(QBQA[0]), .in_4(QBQA[1]), .out_5(\当前楼层 [1]), .out_6(\当前楼层 [0]));
  _7_Segment_Display #(.active("true")) u_7_segment_display_1 (
    .g(multiplexer_1_out[11]), .f(multiplexer_1_out[10]), .a(multiplexer_1_out[9]), .b(multiplexer_1_out[8]),
    .e(multiplexer_1_out_2[11]), .d(multiplexer_1_out_2[10]), .c(multiplexer_1_out_2[9]),
    .dp(multiplexer_1_out_2[8]));
  _7_Segment_Display #(.active("true")) u_7_segment_display_2 (
    .g(multiplexer_1_out[15]), .f(multiplexer_1_out[14]), .a(multiplexer_1_out[13]),
    .b(multiplexer_1_out[12]), .e(multiplexer_1_out_2[15]), .d(multiplexer_1_out_2[14]),
    .c(multiplexer_1_out_2[13]), .dp(multiplexer_1_out_2[12]));
  D_Flip_Flop #(.trigger("rising"), .Pre_Clr_Positions("LEGACY"), .NegatePresetClear("false"), .enable("true"), .NewFFLayout("false")) d_ff_1 (
    .clk(CLK), .D(NEQ), .Q(d_ff_1_q), .Qn(d_ff_1_qn), .en(d_ff_1_qn));  // open: preset, reset
  _7_Segment_Display #(.active("true")) u_7_segment_display_3 (
    .g(multiplexer_1_out[7]), .f(multiplexer_1_out[6]), .a(multiplexer_1_out[5]), .b(multiplexer_1_out[4]),
    .e(multiplexer_1_out_2[7]), .d(multiplexer_1_out_2[6]), .c(multiplexer_1_out_2[5]),
    .dp(multiplexer_1_out_2[4]));
  _7_Segment_Display #(.active("true")) u_7_segment_display_4 (
    .g(multiplexer_1_out[3]), .f(multiplexer_1_out[2]), .a(multiplexer_1_out[1]), .b(multiplexer_1_out[0]),
    .e(multiplexer_1_out_2[3]), .d(multiplexer_1_out_2[2]), .c(multiplexer_1_out_2[1]),
    .dp(multiplexer_1_out_2[0]));
  Multiplexer #(.select(1), .width(32), .disabled(0), .enable("true")) multiplexer_1 (
    .in0(32'h8a66ffee), .in1(32'h8a8cef44), .out({multiplexer_1_out_2, multiplexer_1_out}), .sel(d_ff_1_q),
    .en(halt));

  // Other names for the same wires on the sheet: Equal = _passed; input[3:0] = {\开_关门 , QBQA, \平层 };
  //   Output[1:0] = \当前楼层 ; QA = QBQA[0]; QB = QBQA[1]; tunnel[15:0] = Cnt

  // Notes on the sheet:
  //   测试节拍数
  //   contents of rom_1 (hex, n*v repeats v):
  //   0 0 0 1 0 1 0 2 2 3 2 3 2 4*3 2 0 4 5 4 5 4 5 4 5 5 4 0 8 a b a a a c c d c c d c c
  //   contents of rom_2 (hex, n*v repeats v):
  //   9*0 1 1 2 2 7*3 2 2 1 1
  //   错误记录X&Y
  //   存储器保存未通过的测试用例
  //   ctrl+K驱动时钟自动测试
endmodule

module \电梯控制器  (
  input  \_1楼 ,
  input  \_1楼上 ,
  input  \_2楼下 ,
  input  \_2楼 ,
  input  \_2楼上 ,
  input  \_3楼下 ,
  input  \_3楼 ,
  input  \_3楼上 ,
  input  \_4楼下 ,
  input  \_4楼 ,
  input  \电源 ,
  input  \开门 ,
  input  \关门 ,
  output [6:0] \楼层显示 ,
  output \_1楼上请求 ,
  output \_1楼请求 ,
  output [6:0] \运行计时 ,
  output \_2楼上请求 ,
  output \_2楼请求 ,
  output [6:0] \开门计时 ,
  output \_3楼上请求 ,
  output \_3楼请求 ,
  output \_2楼下请求 ,
  output \_4楼请求 ,
  output \上升 ,
  output \_3楼下请求 ,
  output \下降 ,
  output \_4楼下请求 ,
  output \开_关门 
);

  wire not_1_out, not_2_out, not_3_out, or_1_out, QA, QB, xor_1_out, \上升_t , \下降_t , \平层 , \开门时间到 , \开门请求 ,
       \手动关门请求 , \手动开门请求 , \楼层信号合并_1__1楼有请求 , \楼层信号合并_1__2楼有请求 , \楼层信号合并_1__3楼有请求 , \楼层信号合并_1__4楼有请求 ;
  wire [1:0] \当前楼层 ;
  wire [2:0] \模五计数器_1_out_7 , \模五计数器_2_out_7 ;
  wire [3:0] multiplexer_1_out, multiplexer_2_out, multiplexer_3_out, undriven;

  not not_1 (not_1_out, \开_关门 );
  \楼层计算器  \u_楼层计算器_1  (.in_1(\平层 ), .in_2(not_1_out), .in_3(QA), .in_4(QB), .out_5(\当前楼层 [1]), .out_6(\当前楼层 [0]));
  \开门请求计算  \u_开门请求计算_1  (
    .\楼层低位 (\当前楼层 [0]), .\楼层高位 (\当前楼层 [1]), .\上升 (\上升_t ), .\下降 (\下降_t ), .out_15(\开门请求 ),
    .\内部1楼请求 (\_1楼请求 ), .\_1楼上请求 (\_1楼上请求 ), .\_2楼下请求 (\_2楼下请求 ), .\内部2楼请求 (\_2楼请求 ), .\_2楼上请求 (\_2楼上请求 ),
    .\_3楼下请求 (\_3楼下请求 ), .\内部3楼请求 (\_3楼请求 ), .\_3楼上请求 (\_3楼上请求 ), .\_4楼下请求 (\_4楼下请求 ), .\内部4楼请求 (\_4楼请求 ));
  \请求和取消请求  \u_请求和取消请求_1  (
    .\楼层低位 (\当前楼层 [0]), .\内部1楼请求 (\_1楼 ), .\内部1楼请求_2 (\_1楼请求 ), .\外部1楼上 (\_1楼上 ), .\_1楼上请求 (\_1楼上请求 ),
    .\外部2楼下 (\_2楼下 ), .\_2楼下请求 (\_2楼下请求 ), .\楼层高位 (\当前楼层 [1]), .\内部2楼请求 (\_2楼 ), .\内部2楼请求_2 (\_2楼请求 ),
    .\外部2楼上 (\_2楼上 ), .\_2楼上请求 (\_2楼上请求 ), .\外部3楼下 (\_3楼下 ), .\_3楼下请求 (\_3楼下请求 ), .\内部3楼请求 (\_3楼 ),
    .\内部3楼请求_2 (\_3楼请求 ), .\上升 (\上升_t ), .\内部4楼请求 (\_4楼 ), .\内部4楼请求_2 (\_4楼请求 ), .\外部3楼上 (\_3楼上 ),
    .\_3楼上请求 (\_3楼上请求 ), .\外部4楼下 (\_4楼下 ), .\_4楼下请求 (\_4楼下请求 ), .\下降 (\下降_t ), .\开门 (\开_关门 ), .\开门_2 (\开门 ),
    .\关门 (\关门 ), .\手动开门请求 (\手动开门请求 ), .\手动关门请求 (\手动关门请求 ));
  \七段数码管  \u_七段数码管_1  (
    .X3(multiplexer_1_out[3]), .X2(multiplexer_1_out[2]), .Seg_1(\楼层显示 [0]), .X1(multiplexer_1_out[1]),
    .X0(multiplexer_1_out[0]), .Seg_2(\楼层显示 [1]), .Seg_3(\楼层显示 [2]), .Seg_4(\楼层显示 [3]), .Seg_5(\楼层显示 [4]),
    .Seg_6(\楼层显示 [5]), .Seg_7(\楼层显示 [6]));
  Multiplexer #(.select(2), .width(4), .disabled("Z"), .enable("false")) multiplexer_1 (
    .in0(4'b0001), .in1(4'b0010), .in2(4'b0011), .in3(4'b0100), .out(multiplexer_1_out), .sel(\当前楼层 ));
  and and_1 (\上升 , QA, not_2_out);
  not not_2 (not_2_out, QB);
  not not_3 (not_3_out, QA);
  and and_2 (\下降 , not_3_out, QB);
  \电梯上下停开状态转移  \u_电梯上下停开状态转移_1  (
    .\手动关门 (\手动关门请求 ), .\上升 (\上升_t ), .\手动开门 (\手动开门请求 ), .\下降 (\下降_t ), .\其他输入引起的开门请求 (\开门请求 ),
    .\开门时间到 (\开门时间到 ), .\开门 (\开_关门 ), .out_8(QA), .out_9(QB));
  \楼层信号合并  \u_楼层信号合并_1  (
    .\_1楼有请求 (\楼层信号合并_1__1楼有请求 ), .\_1楼上请求 (\_1楼上请求 ), .\_2楼下请求 (\_2楼下请求 ), .\_2楼有请求 (\楼层信号合并_1__2楼有请求 ),
    .\_2楼上请求 (\_2楼上请求 ), .\_3楼下请求 (\_3楼下请求 ), .\_3楼有请求 (\楼层信号合并_1__3楼有请求 ), .\_3楼上请求 (\_3楼上请求 ),
    .\_4楼下请求 (\_4楼下请求 ), .\_4楼有请求 (\楼层信号合并_1__4楼有请求 ), .\内部1楼请求 (\_1楼请求 ), .\内部2楼请求 (\_2楼请求 ),
    .\内部3楼请求 (\_3楼请求 ), .\内部4楼请求 (\_4楼请求 ));
  xor xor_1 (xor_1_out, QA, QB);
  or or_1 (or_1_out, \开门 , \关门 );
  \模五计数器  \u_模五计数器_1  (
    .in_1(xor_1_out), .in_2(\电源 ), .\零 (\平层 ), .out_5(\模五计数器_1_out_7 [2]), .out_6(\模五计数器_1_out_7 [1]),
    .out_7(\模五计数器_1_out_7 [0]), .in_3(\开_关门 ));
  \模五计数器  \u_模五计数器_2  (
    .in_1(\开_关门 ), .in_2(\电源 ), .\零 (\开门时间到 ), .out_5(\模五计数器_2_out_7 [2]), .out_6(\模五计数器_2_out_7 [1]),
    .out_7(\模五计数器_2_out_7 [0]), .in_3(or_1_out));
  \电梯上下停状态转移  \u_电梯上下停状态转移_1  (
    .\_1楼有请求 (\楼层信号合并_1__1楼有请求 ), .\_2楼有请求 (\楼层信号合并_1__2楼有请求 ), .\楼层低位 (\当前楼层 [0]),
    .\_3楼有请求 (\楼层信号合并_1__3楼有请求 ), .\楼层高位 (\当前楼层 [1]), .\_4楼有请求 (\楼层信号合并_1__4楼有请求 ), .\上升 (\上升_t ),
    .\下降 (\下降_t ));
  Multiplexer #(.select(3), .width(4), .disabled("Z"), .enable("false")) multiplexer_2 (
    .in0(4'b0101), .in1(4'b0100), .in2(4'b0011), .in3(4'b0010), .in4(4'b0001), .in5(undriven),
    .in6(undriven), .out(multiplexer_2_out), .sel(\模五计数器_2_out_7 ));  // open: in7
  Multiplexer #(.select(3), .width(4), .disabled("Z"), .enable("false")) multiplexer_3 (
    .in0(4'b0101), .in1(4'b0100), .in2(4'b0011), .in3(4'b0010), .in4(4'b0001), .out(multiplexer_3_out),
    .sel(\模五计数器_1_out_7 ));  // open: in5, in6, in7
  \七段数码管  \u_七段数码管_2  (
    .X3(multiplexer_2_out[3]), .X2(multiplexer_2_out[2]), .Seg_1(\开门计时 [0]), .X1(multiplexer_2_out[1]),
    .X0(multiplexer_2_out[0]), .Seg_2(\开门计时 [1]), .Seg_3(\开门计时 [2]), .Seg_4(\开门计时 [3]), .Seg_5(\开门计时 [4]),
    .Seg_6(\开门计时 [5]), .Seg_7(\开门计时 [6]));
  \七段数码管  \u_七段数码管_3  (
    .X3(multiplexer_3_out[3]), .X2(multiplexer_3_out[2]), .Seg_1(\运行计时 [0]), .X1(multiplexer_3_out[1]),
    .X0(multiplexer_3_out[0]), .Seg_2(\运行计时 [1]), .Seg_3(\运行计时 [2]), .Seg_4(\运行计时 [3]), .Seg_5(\运行计时 [4]),
    .Seg_6(\运行计时 [5]), .Seg_7(\运行计时 [6]));

  // Other names for the same wires on the sheet: 手动关门 = \关门 ; 手动开门 = \开门 

  // Notes on the sheet:
  //   内部输入
  //   外部输入
  //   输出
endmodule

module \总电路测试  (
  input  \电源 
);

  wire \_1楼 , \_1楼上 , \_1楼上请求 , \_1楼请求 , \_2楼 , \_2楼上 , \_2楼上请求 , \_2楼下 , \_2楼下请求 , \_2楼请求 , \_3楼 , \_3楼上 ,
       \_3楼上请求 , \_3楼下 , \_3楼下请求 , \_3楼请求 , \_4楼 , \_4楼下 , \_4楼下请求 , \_4楼请求 , \上升 , \下降 , \开_关门 , \手动关门 ,
       \手动开门 ;
  wire [6:0] \开门计时 , \楼层显示 , \运行计时 ;

  Button \u__1楼  (.out(\_1楼 ));
  Button \u__2楼  (.out(\_2楼 ));
  Button \u__3楼  (.out(\_3楼 ));
  Button \u__4楼  (.out(\_4楼 ));
  Button \u_开门  (.out(\手动开门 ));
  LED #(.active("true")) led_1 (.in(\_1楼请求 ));
  LED #(.active("true")) led_2 (.in(\_2楼请求 ));
  LED #(.active("true")) led_3 (.in(\_3楼请求 ));
  LED #(.active("true")) led_4 (.in(\_4楼请求 ));
  Button \u_关门  (.out(\手动关门 ));
  Button \u__1楼上  (.out(\_1楼上 ));
  Button \u__2楼上  (.out(\_2楼上 ));
  Button \u__3楼上  (.out(\_3楼上 ));
  LED #(.active("true")) led_5 (.in(\_1楼上请求 ));
  LED #(.active("true")) led_6 (.in(\_2楼上请求 ));
  LED #(.active("true")) led_7 (.in(\_3楼上请求 ));
  \电梯控制器  \u_电梯控制器_1  (
    .\电源 (\电源 ), .\_1楼 (\_1楼 ), .\_2楼 (\_2楼 ), .\_3楼 (\_3楼 ), .\_4楼 (\_4楼 ), .\开门 (\手动开门 ), .\关门 (\手动关门 ),
    .\_1楼上 (\_1楼上 ), .\_2楼上 (\_2楼上 ), .\_3楼上 (\_3楼上 ), .\_2楼下 (\_2楼下 ), .\_3楼下 (\_3楼下 ), .\_4楼下 (\_4楼下 ),
    .\开_关门 (\开_关门 ), .\上升 (\上升 ), .\下降 (\下降 ), .\楼层显示 (\楼层显示 ), .\运行计时 (\运行计时 ), .\开门计时 (\开门计时 ),
    .\_1楼上请求 (\_1楼上请求 ), .\_2楼上请求 (\_2楼上请求 ), .\_3楼上请求 (\_3楼上请求 ), .\_2楼下请求 (\_2楼下请求 ), .\_3楼下请求 (\_3楼下请求 ),
    .\_4楼下请求 (\_4楼下请求 ), .\_1楼请求 (\_1楼请求 ), .\_2楼请求 (\_2楼请求 ), .\_3楼请求 (\_3楼请求 ), .\_4楼请求 (\_4楼请求 ));
  Button \u__2楼下  (.out(\_2楼下 ));
  Button \u__3楼下  (.out(\_3楼下 ));
  Button \u__4楼下  (.out(\_4楼下 ));
  LED #(.active("true")) led_8 (.in(\_2楼下请求 ));
  LED #(.active("true")) led_9 (.in(\_3楼下请求 ));
  LED #(.active("true")) led_10 (.in(\_4楼下请求 ));
  LED #(.active("true")) \u_开门指示灯  (.in(\开_关门 ));
  _7_Segment_Display #(.active("true")) u_7_segment_display_1 (
    .g(\楼层显示 [0]), .f(\楼层显示 [1]), .a(\楼层显示 [2]), .b(\楼层显示 [3]), .e(\楼层显示 [4]), .d(\楼层显示 [5]), .c(\楼层显示 [6]));  // open: dp
  _7_Segment_Display #(.active("true")) u_7_segment_display_2 (
    .g(\运行计时 [0]), .f(\运行计时 [1]), .a(\运行计时 [2]), .b(\运行计时 [3]), .e(\运行计时 [4]), .d(\运行计时 [5]), .c(\运行计时 [6]));  // open: dp
  LED #(.active("true")) \u_上升指示灯  (.in(\上升 ));
  LED #(.active("true")) \u_下降指示灯  (.in(\下降 ));
  _7_Segment_Display #(.active("true")) u_7_segment_display_3 (
    .g(\开门计时 [0]), .f(\开门计时 [1]), .a(\开门计时 [2]), .b(\开门计时 [3]), .e(\开门计时 [4]), .d(\开门计时 [5]), .c(\开门计时 [6]));  // open: dp

  // Notes on the sheet:
  //   内部输入
  //   外部输入
  //   楼层
  //   输出
  //   运行计时
  //   开门计时
endmodule
